// Logisim project processador.circ as structural Verilog: 7 circuits, main circuit ProgramCounter
module ProgramCounter (
  input  [7:0] data,
  input  W_PC,
  input  Clk,
  input  Reset,
  output [7:0] Pc_mais_1,
  output [7:0] Pc_out
);

  Register register_1 (.D(data), .en(W_PC), .clk(Clk), .Q(Pc_out), .clr(Reset));
  Adder adder_1 (.a(Pc_out), .b(8'h1), .out(Pc_mais_1));  // open: cin, cout
endmodule

module Main (
  input  MANUAL_RESET_RG,
  input  MANUAL_RESET
);

  wire B, branches_1_b_out, clk, IMM_ULA, or_1_out, or_2_out, RESET, W_MEM, W_PC, W_RG;
  wire [1:0] B_IN, D_RG, multiplexer_2_out, PC_M, rom_1_data, rom_1_data_2;
  wire [2:0] OP_ULA;
  wire [3:0] rom_1_data_3;
  wire [7:0] Imm, mem_out, multiplexer_1_out, multiplexer_3_out, multiplexer_4_out, pc_imm, Pc_mais_1,
       programcounter_1_pc_out, RA_OUT, RB_OUT, rs1_imm;
  wire [31:0] rs1_out, rs2_out;

  Multiplexer #(.select(2), .width(8)) multiplexer_1 (
    .in0(Pc_mais_1), .in1(pc_imm), .in2(rs1_imm), .out(multiplexer_1_out), .sel(multiplexer_2_out));  // open: in3
  Multiplexer #(.width(2)) multiplexer_2 (.in0(PC_M), .in1(2'b01), .out(multiplexer_2_out), .sel(branches_1_b_out));
  or or_1 (or_1_out, MANUAL_RESET, RESET);
  branches branches_1 (.rs1(rs1_out), .rs2(rs2_out), .B_in(B_IN), .B(B), .B_out(branches_1_b_out));
  Clock clock_1 (.out(clk));
  ProgramCounter programcounter_1 (
    .data(multiplexer_1_out), .W_PC(W_PC), .Clk(clk), .Reset(or_1_out), .Pc_mais_1(Pc_mais_1),
    .Pc_out(programcounter_1_pc_out));
  Adder adder_1 (.a(programcounter_1_pc_out), .b(Imm), .out(pc_imm));  // open: cin, cout
  dual_port_ram dual_port_ram_1 ();  // open: addr, pc, d, w, instr, data
  ROM rom_1 (.addr(programcounter_1_pc_out), .data({rom_1_data_3, rom_1_data_2, rom_1_data}));
  assign Imm = {{4{rom_1_data_2[1]}}, {rom_1_data_2, rom_1_data}};  // Bit_Extender bit_extender_1
  or or_2 (or_2_out, MANUAL_RESET_RG, RESET);
  banco_reg banco_reg_1 (
    .rb(rom_1_data_2), .CLK(clk), .D(multiplexer_3_out), .Reset(or_2_out), .ra(rom_1_data), .WE(W_RG),
    .RA_OUT(RA_OUT), .RB_OUT(RB_OUT));
  unit_control unit_control_1 (
    .OpCode(rom_1_data_3), .IMM_ULA(IMM_ULA), .W_RG(W_RG), .W_MEM(W_MEM), .PC_M(PC_M), .B(B), .D_RG(D_RG),
    .B_IN(B_IN), .OP_ULA(OP_ULA), .W_PC(W_PC), .RESET(RESET));
  Multiplexer #(.select(2), .width(8)) multiplexer_3 (
    .in0(rs1_imm), .in1(mem_out), .in2(Pc_mais_1), .out(multiplexer_3_out), .sel(D_RG));  // open: in3
  Multiplexer #(.width(8)) multiplexer_4 (.in0(RB_OUT), .in1(Imm), .out(multiplexer_4_out), .sel(IMM_ULA));
  ULA ula_1 (.RA(RA_OUT), .RB(multiplexer_4_out), .op_ula(OP_ULA), .D(rs1_imm));
  RAM ram_1 (.addr(rs1_imm), .we(W_MEM), .oe(1'b1), .clk(clk), .din(RB_OUT), .dout(mem_out));

  // Other names for the same wires on the sheet: Ula_result[7:0] = rs1_imm
endmodule

module banco_reg (
  input  Reset,
  input  CLK,
  input  [7:0] D,
  input  [1:0] ra,
  input  WE,
  input  [1:0] rb,
  output [7:0] RA_OUT,
  output [7:0] RB_OUT
);

  wire demultiplexer_1_out0, demultiplexer_1_out1, demultiplexer_1_out2, demultiplexer_1_out3;
  wire [7:0] R0, R1, R2, R3;

  Demultiplexer #(.select(2)) demultiplexer_1 (
    .out0(demultiplexer_1_out0), .out1(demultiplexer_1_out1), .out2(demultiplexer_1_out2),
    .out3(demultiplexer_1_out3), .in(WE), .sel(ra));
  Register u_R0 (.D(D), .en(demultiplexer_1_out0), .clk(CLK), .Q(R0), .clr(Reset));
  Register u_R1 (.D(D), .en(demultiplexer_1_out1), .clk(CLK), .Q(R1), .clr(Reset));
  Register u_R2 (.D(D), .en(demultiplexer_1_out2), .clk(CLK), .Q(R2), .clr(Reset));
  Register u_R3 (.D(D), .en(demultiplexer_1_out3), .clk(CLK), .Q(R3), .clr(Reset));
  Multiplexer #(.select(2), .width(8)) multiplexer_1 (.in0(R0), .in1(R1), .in2(R2), .in3(R3), .out(RA_OUT), .sel(ra));
  Multiplexer #(.select(2), .width(8)) multiplexer_2 (.in0(R0), .in1(R1), .in2(R2), .in3(R3), .out(RB_OUT), .sel(rb));

  // Other names for the same wires on the sheet: CLK_t = CLK; D_t[7:0] = D; R_t = Reset
endmodule

module ULA (
  input  [7:0] RA,
  input  [7:0] RB,
  input  [2:0] op_ula,
  output [7:0] D
);

  wire [7:0] adder_1_out, and_1_out, or_1_out, subtractor_1_out;

  assign and_1_out = RA & RB;  // AND_Gate and_1, 8 bits wide
  assign or_1_out = RA | RB;  // OR_Gate or_1, 8 bits wide
  Adder adder_1 (.a(RA), .b(RB), .out(adder_1_out));  // open: cin, cout
  Subtractor subtractor_1 (.a(RA), .b(RB), .out(subtractor_1_out));  // open: bin, bout
  Multiplexer #(.select(3), .width(8)) multiplexer_1 (
    .in0(adder_1_out), .in1(subtractor_1_out), .in3(and_1_out), .in4(or_1_out), .out(D), .sel(op_ula));  // open: in2, in5, in6, in7
endmodule

module branches (
  input  [31:0] rs1,
  input  [31:0] rs2,
  input  B,
  input  [1:0] B_in,
  output B_out
);

  wire comparator_1_eq, comparator_1_gt, comparator_1_lt, not_1_out, or_1_out;

  Comparator #(.width(32)) comparator_1 (
    .a(rs1), .b(rs2), .gt(comparator_1_gt), .eq(comparator_1_eq), .lt(comparator_1_lt));
  or or_1 (or_1_out, comparator_1_gt, comparator_1_eq);
  not not_1 (not_1_out, comparator_1_eq);
  Multiplexer #(.enable("true"), .select(2)) multiplexer_1 (
    .in0(comparator_1_eq), .in1(comparator_1_lt), .in2(not_1_out), .in3(or_1_out), .out(B_out), .sel(B_in),
    .en(B));
endmodule

module unit_control (
  input  [3:0] OpCode,
  output IMM_ULA,
  output W_RG,
  output W_MEM,
  output [1:0] PC_M,
  output B,
  output [1:0] D_RG,
  output [1:0] B_IN,
  output [2:0] OP_ULA,
  output W_PC,
  output RESET
);

  wire and_1_out, and_2_out, and_4_out, and_5_out, and_6_out, and_7_out, and_10_out, and_11_out, and_12_out,
       and_13_out, and_15_out, and_23_out, or_1_out, or_2_out, or_3_out, or_5_out, S1_N, S2_N, S3_N, S4_N;

  not not_1 (S1_N, OpCode[0]);
  not not_2 (S2_N, OpCode[1]);
  not not_3 (S3_N, OpCode[2]);
  not not_4 (S4_N, OpCode[3]);
  and and_1 (and_1_out, S3_N, OpCode[3]);
  and and_2 (and_2_out, OpCode[0], OpCode[1], OpCode[2], S4_N);
  and and_3 (B, S3_N, OpCode[3]);
  and and_4 (and_4_out, S2_N, S3_N);
  and and_5 (and_5_out, OpCode[1], S3_N);
  and and_6 (and_6_out, S2_N, OpCode[2]);
  and and_7 (and_7_out, OpCode[1], OpCode[2]);
  or or_1 (or_1_out, and_1_out, and_2_out);
  not not_5 (W_RG, or_1_out);
  and and_8 (D_RG[0], S1_N, OpCode[1], OpCode[2], S4_N);
  and and_9 (D_RG[1], S2_N, OpCode[2], S4_N);
  and and_10 (and_10_out, OpCode[1], S3_N, S4_N);
  or or_2 (or_2_out, and_10_out, and_11_out);
  and and_11 (and_11_out, S2_N, OpCode[2], OpCode[3]);
  and and_12 (and_12_out, OpCode[0], OpCode[1], S3_N, S4_N);
  and and_13 (and_13_out, S1_N, S2_N, OpCode[2], OpCode[3]);
  and and_14 (OP_ULA[2], OpCode[0], S2_N, OpCode[2], OpCode[3]);
  or or_3 (or_3_out, and_4_out, and_5_out, and_6_out);
  and and_15 (and_15_out, or_3_out, OpCode[0]);
  and and_16 (OP_ULA[0], S1_N, or_2_out);
  or or_4 (OP_ULA[1], and_12_out, and_13_out);
  or or_5 (or_5_out, and_15_out, and_7_out);
  and and_17 (IMM_ULA, or_5_out, S4_N);
  and and_18 (W_MEM, OpCode[0], OpCode[1], OpCode[2], S4_N);
  and and_19 (PC_M[0], S4_N, OpCode[2], S2_N, S1_N);
  and and_20 (PC_M[1], S4_N, OpCode[2], S2_N, OpCode[0]);
  and and_21 (B_IN[0], OpCode[3], S3_N, OpCode[1]);
  and and_22 (B_IN[1], OpCode[3], S3_N, OpCode[0]);
  and and_23 (and_23_out, S1_N, OpCode[1], OpCode[2], OpCode[3]);
  and and_24 (RESET, OpCode[0], OpCode[1], OpCode[2], OpCode[3]);
  not not_6 (W_PC, and_23_out);

  // Other names for the same wires on the sheet: S1 = OpCode[0]; S2 = OpCode[1]; S3 = OpCode[2]; S4 = OpCode[3]
endmodule

module dual_port_ram (
  input  [7:0] addr,
  input  [7:0] pc,
  input  [7:0] d,
  input  w,
  output [7:0] instr,
  output [7:0] data
);

  wire clock_1_out, or_1_out;
  wire [7:0] multiplexer_1_out;

  Clock clock_1 (.out(clock_1_out));
  or or_1 (or_1_out, w, clock_1_out);
  Multiplexer #(.width(8)) multiplexer_1 (.in0(addr), .in1(pc), .out(multiplexer_1_out), .sel(clock_1_out));
  RAM #(.asyncread("true")) ram_1 (
    .addr(multiplexer_1_out), .we(or_1_out), .oe(1'b1), .clk(clock_1_out), .din(d), .dout(data));
  Register #(.trigger("falling")) pcbuf (.D(data), .en(1'b1), .clk(clock_1_out), .Q(instr));  // open: clr
endmodule
