// Logisim project stable1.circ as structural Verilog
module ProgramCounter (
  input  [7:0] data,
  input  Clk,
  input  Reset,
  output [7:0] Pc_mais_1,
  output [7:0] Pc_out
);

  Register register_1 (.D(data), .en(1'b1), .clk(Clk), .Q(Pc_out), .clr(Reset));
  Adder adder_1 (.a(Pc_out), .b(8'h1), .out(Pc_mais_1));  // open: cin, cout
endmodule

module Main (
  input  MANUAL_RESET_RG,
  input  in_2,
  input  MANUAL_RESET
);

  wire ADDI, and_1_out, BRZR, clk, IMM_ULA, JI, LOAD, or_1_out, or_2_out, W_MEM, W_RG, ZERO;
  wire [1:0] bit_extender_1_out, multiplexer_1_out, multiplexer_3_out, rom_1_data, rom_1_data_2;
  wire [2:0] OP_ULA;
  wire [3:0] rom_1_data_3;
  wire [7:0] Imm, mem_out, multiplexer_2_out, multiplexer_4_out, multiplexer_5_out, multiplexer_6_out, PC,
       Pc_mais_1, RA_OUT, RB_OUT, Ula_result;

  assign bit_extender_1_out = {{1{and_1_out}}, and_1_out};  // Bit_Extender bit_extender_1
  and and_1 (and_1_out, BRZR, ZERO);
  Multiplexer #(.width(2)) multiplexer_1 (.in0(bit_extender_1_out), .in1(2'b01), .out(multiplexer_1_out), .sel(JI));
  Multiplexer #(.select(2), .width(8)) multiplexer_2 (
    .in0(Pc_mais_1), .in1(Ula_result), .in3(RB_OUT), .out(multiplexer_2_out), .sel(multiplexer_1_out));  // open: in2
  or or_1 (or_1_out, MANUAL_RESET, in_2);
  Clock clock_1 (.out(clk));
  ProgramCounter programcounter_1 (
    .data(multiplexer_2_out), .Clk(clk), .Reset(or_1_out), .Pc_mais_1(Pc_mais_1), .Pc_out(PC));
  dual_port_ram dual_port_ram_1 ();  // open: addr, pc, d, w, instr, data
  ROM rom_1 (.addr(PC), .data({rom_1_data_3, rom_1_data_2, rom_1_data}));
  Multiplexer #(.width(2)) multiplexer_3 (.in0(rom_1_data_2), .in1(2'b00), .out(multiplexer_3_out), .sel(ADDI));
  ROM #(.addrWidth(4), .dataWidth(10)) rom_2 (
    .addr(rom_1_data_3), .data({LOAD, BRZR, JI, ADDI, W_MEM, IMM_ULA, OP_ULA, W_RG}));
  assign Imm = {{4{rom_1_data_2[1]}}, {rom_1_data_2, rom_1_data}};  // Bit_Extender bit_extender_2
  or or_2 (or_2_out, MANUAL_RESET_RG, in_2);
  banco_reg banco_reg_1 (
    .rb(rom_1_data), .CLK(clk), .D(multiplexer_4_out), .Reset(or_2_out), .ra(multiplexer_3_out), .WE(W_RG),
    .RA_OUT(RA_OUT), .RB_OUT(RB_OUT));
  Multiplexer #(.width(8)) multiplexer_4 (.in0(Ula_result), .in1(mem_out), .out(multiplexer_4_out), .sel(LOAD));
  RAM #(.asyncread("true")) ram_1 (.addr(RB_OUT), .we(W_MEM), .oe(1'b1), .clk(clk), .din(RA_OUT), .dout(mem_out));
  Multiplexer #(.width(8)) multiplexer_5 (.in0(RA_OUT), .in1(PC), .out(multiplexer_5_out), .sel(JI));
  Multiplexer #(.width(8)) multiplexer_6 (.in0(RB_OUT), .in1(Imm), .out(multiplexer_6_out), .sel(IMM_ULA));
  ULA ula_1 (.op_ula(OP_ULA), .RA(multiplexer_5_out), .RB(multiplexer_6_out), .D(Ula_result), .ZERO(ZERO));

  // Other names for the same wires on the sheet: RESET = in_2

  // Notes on the sheet:
  //   PC + IMM
  //   contents of rom_1 (hex, n*v repeats v):
  //   47 c8 4d e8 4b 40 38 46 45 c4 d0 4d 34 4f 34 4f c5 34 d0 4e cc d9 47 45 d8 3b d0 d5 41 c4 4e 20 47
  //   42 df cc d0 da 46 c8 4d e8 41 c8 d0 4b 20 4e 33 dd 2 1c da 44 e0 43 c8 d0 4b 20 cc 4f 33 dd 4f 2 1b
  //   4d 24 4e 20 cc d0 4e 28 d0 33 41 dc d4 6 1a d0 4f 2c 42 cc 4e 3c 42 dc 4b 20 27 cc 2b c6 cc 37 d0 4d
  //   24 44 d4 4c 34 85 41 28 6 c0 d0 112*0 11
  //   contents of rom_2 (hex, n*v repeats v):
  //   100 98 201 20 59 0 0 0 1 3 5 7 9 b d f
endmodule

module banco_reg (
  input  Reset,
  input  CLK,
  input  [7:0] D,
  input  [1:0] ra,
  input  WE,
  input  [1:0] rb,
  output [7:0] RA_OUT,
  output [7:0] RB_OUT
);

  wire demultiplexer_1_out0, demultiplexer_1_out1, demultiplexer_1_out2, demultiplexer_1_out3;
  wire [7:0] R0, R1, R2, R3;

  Demultiplexer #(.select(2)) demultiplexer_1 (
    .out0(demultiplexer_1_out0), .out1(demultiplexer_1_out1), .out2(demultiplexer_1_out2),
    .out3(demultiplexer_1_out3), .in(WE), .sel(ra));
  Register u_R0 (.D(D), .en(demultiplexer_1_out0), .clk(CLK), .Q(R0), .clr(Reset));
  Register u_R1 (.D(D), .en(demultiplexer_1_out1), .clk(CLK), .Q(R1), .clr(Reset));
  Register u_R2 (.D(D), .en(demultiplexer_1_out2), .clk(CLK), .Q(R2), .clr(Reset));
  Register u_R3 (.D(D), .en(demultiplexer_1_out3), .clk(CLK), .Q(R3), .clr(Reset));
  Multiplexer #(.select(2), .width(8)) multiplexer_1 (.in0(R0), .in1(R1), .in2(R2), .in3(R3), .out(RA_OUT), .sel(ra));
  Multiplexer #(.select(2), .width(8)) multiplexer_2 (.in0(R0), .in1(R1), .in2(R2), .in3(R3), .out(RB_OUT), .sel(rb));

  // Other names for the same wires on the sheet: CLK_t = CLK; D_t[7:0] = D; R_t = Reset
endmodule

module ULA (
  input  [7:0] RA,
  input  [7:0] RB,
  input  [2:0] op_ula,
  output [7:0] D,
  output ZERO
);

  wire comparator_1_eq;
  wire [2:0] bit_extender_1_out;
  wire [7:0] adder_1_out, and_1_out, bit_extender_2_out, or_1_out, shifter_1_out, shifter_2_out,
       subtractor_1_out, xor_1_out;

  Bit_Extender #(.out_width(3)) bit_extender_1 (.in(RB), .out(bit_extender_1_out));
  assign and_1_out = RA & RB;  // AND_Gate and_1, 8 bits wide
  assign or_1_out = RA | RB;  // OR_Gate or_1, 8 bits wide
  Comparator comparator_1 (.a({8{1'b0}}), .b(RB), .eq(comparator_1_eq));  // open: gt, lt
  assign xor_1_out = RA ^ RB;  // XOR_Gate xor_1, 8 bits wide
  Adder adder_1 (.a(RA), .b(RB), .out(adder_1_out));  // open: cin, cout
  Subtractor subtractor_1 (.a(RA), .b(RB), .out(subtractor_1_out));  // open: bin, bout
  Shifter shifter_1 (.in(RA), .\dist (bit_extender_1_out), .out(shifter_1_out));
  Shifter #(.shift("lr")) shifter_2 (.in(RA), .\dist (bit_extender_1_out), .out(shifter_2_out));
  Comparator comparator_2 (.a(RA), .b({8{1'b0}}), .eq(ZERO));  // open: gt, lt
  assign bit_extender_2_out = {{7{1'b0}}, comparator_1_eq};  // Bit_Extender bit_extender_2
  Multiplexer #(.select(3), .width(8)) multiplexer_1 (
    .in0(bit_extender_2_out), .in1(and_1_out), .in2(or_1_out), .in3(xor_1_out), .in4(adder_1_out),
    .in5(subtractor_1_out), .in6(shifter_1_out), .in7(shifter_2_out), .out(D), .sel(op_ula));
endmodule

module branches (
  input  [31:0] rs1,
  input  [31:0] rs2,
  input  B,
  input  [1:0] B_in,
  output B_out
);

  wire comparator_1_eq, comparator_1_gt, comparator_1_lt, not_1_out, or_1_out;

  Comparator #(.width(32)) comparator_1 (
    .a(rs1), .b(rs2), .gt(comparator_1_gt), .eq(comparator_1_eq), .lt(comparator_1_lt));
  or or_1 (or_1_out, comparator_1_gt, comparator_1_eq);
  not not_1 (not_1_out, comparator_1_eq);
  Multiplexer #(.enable("true"), .select(2)) multiplexer_1 (
    .in0(comparator_1_eq), .in1(comparator_1_lt), .in2(not_1_out), .in3(or_1_out), .out(B_out), .sel(B_in),
    .en(B));
endmodule

module dual_port_ram (
  input  [7:0] addr,
  input  [7:0] pc,
  input  [7:0] d,
  input  w,
  output [7:0] instr,
  output [7:0] data
);

  wire clock_1_out, or_1_out;
  wire [7:0] multiplexer_1_out;

  Clock clock_1 (.out(clock_1_out));
  or or_1 (or_1_out, w, clock_1_out);
  Multiplexer #(.width(8)) multiplexer_1 (.in0(addr), .in1(pc), .out(multiplexer_1_out), .sel(clock_1_out));
  RAM #(.asyncread("true")) ram_1 (
    .addr(multiplexer_1_out), .we(or_1_out), .oe(1'b1), .clk(clock_1_out), .din(d), .dout(data));
  Register #(.trigger("falling")) pcbuf (.D(data), .en(1'b1), .clk(clock_1_out), .Q(instr));  // open: clr
endmodule
