// Logisim project processador.circ as structural Verilog
module ProgramCounter (
  input  [7:0] data,
  input  Clk,
  input  Reset,
  output [7:0] Pc_mais_1,
  output [7:0] Pc_out
);

  Register register_1 (.D(data), .en(1'b1), .clk(Clk), .Q(Pc_out), .clr(Reset));
  Adder adder_1 (.a(Pc_out), .b(8'h1), .out(Pc_mais_1));  // open: cin, cout
endmodule

module Main (
  input  MANUAL_RESET_RG,
  input  in_2,
  input  MANUAL_RESET
);

  wire ADD_V, ADD_V_EXEC, ADDI, and_1_out, and_2_out, and_3_out, and_4_out, and_5_out, and_6_out, and_8_out,
       BRZR, CLK, comparator_1_eq, comparator_2_eq, IMM_ULA, INC, INC_ALL, JI, LOAD, LOAD_V, LOAD_V_EXEC,
       MICRO_CODE_EXECUTING, not_1_out, not_4_out, or_1_out, or_2_out, or_3_out, or_4_out, or_6_out,
       or_7_out, W_MEM, W_RG, ZERO;
  wire [1:0] bit_extender_1_out, multiplexer_1_out, multiplexer_9_out;
  wire [2:0] OP_ULA;
  wire [7:0] dual_port_ram_1_instr, IMM, MEM_OUT, multiplexer_2_out, multiplexer_3_out, multiplexer_4_out,
       multiplexer_5_out, multiplexer_6_out, multiplexer_7_out, multiplexer_8_out, multiplexer_10_out,
       multiplexer_11_out, multiplexer_12_out, multiplexer_13_out, multiplexer_14_out, multiplexer_15_out,
       multiplexer_16_out, PC, PC_2, PC_2_MAIS_1, PC_PLUS_1, RA_OUT, RB_IMM, RB_OUT, register_1_q,
       register_2_q, rom_1_data, subtractor_1_out, subtractor_2_out, UINT, ULA_OUT, x_out, y_out;

  and and_1 (and_1_out, BRZR, ZERO);
  assign bit_extender_1_out = {{1{and_1_out}}, and_1_out};  // Bit_Extender bit_extender_1
  and and_2 (and_2_out, JI, not_1_out);
  Multiplexer #(.width(2)) multiplexer_1 (
    .in0(bit_extender_1_out), .in1(2'b01), .out(multiplexer_1_out), .sel(and_2_out));
  Multiplexer #(.select(2), .width(8)) multiplexer_2 (
    .in0(PC_PLUS_1), .in1(ULA_OUT), .in3(RB_OUT), .out(multiplexer_2_out), .sel(multiplexer_1_out));  // open: in2
  Multiplexer #(.width(8)) multiplexer_3 (.in0(PC_2_MAIS_1), .in1(ULA_OUT), .out(multiplexer_3_out), .sel(JI));
  or or_1 (or_1_out, MICRO_CODE_EXECUTING, ADD_V, LOAD_V);
  Subtractor subtractor_1 (.a(register_1_q), .b(8'h1), .out(subtractor_1_out));  // open: bin, bout
  and and_3 (and_3_out, LOAD_V_EXEC, JI);
  not not_1 (not_1_out, MICRO_CODE_EXECUTING);
  Multiplexer #(.width(8)) multiplexer_4 (.in0({8{1'b0}}), .in1(8'h5), .out(multiplexer_4_out), .sel(ADD_V));
  Register #(.trigger("falling")) register_1 (
    .D(multiplexer_5_out), .en(or_2_out), .clk(CLK), .Q(register_1_q), .clr(in_2));
  Multiplexer #(.width(8)) multiplexer_5 (.in0(subtractor_1_out), .in1(UINT), .out(multiplexer_5_out), .sel(LOAD_V));
  or or_2 (or_2_out, and_3_out, LOAD_V);
  and and_4 (and_4_out, CLK, not_1_out);
  or or_3 (or_3_out, MANUAL_RESET, in_2);
  or or_4 (or_4_out, LOAD_V, ADD_V);
  Multiplexer #(.width(8)) multiplexer_6 (
    .in0(multiplexer_3_out), .in1(multiplexer_4_out), .out(multiplexer_6_out), .sel(or_4_out));
  and and_5 (and_5_out, CLK, or_1_out);
  Clock #(.highDuration(2), .lowDuration(2)) clock_1 (.out(CLK));
  not not_2 (LOAD_V_EXEC, comparator_1_eq);
  Comparator comparator_1 (.a(register_1_q), .b({8{1'b0}}), .eq(comparator_1_eq));  // open: gt, lt
  ProgramCounter programcounter_1 (
    .data(multiplexer_2_out), .Clk(and_4_out), .Reset(or_3_out), .Pc_mais_1(PC_PLUS_1), .Pc_out(PC));
  ProgramCounter programcounter_2 (
    .data(multiplexer_6_out), .Clk(and_5_out), .Reset(in_2), .Pc_mais_1(PC_2_MAIS_1), .Pc_out(PC_2));
  or or_5 (MICRO_CODE_EXECUTING, LOAD_V_EXEC, ADD_V_EXEC);
  ROM rom_1 (.addr(PC_2), .data(rom_1_data));
  and and_6 (and_6_out, ADD_V_EXEC, JI);
  Subtractor subtractor_2 (.a(register_2_q), .b(8'h1), .out(subtractor_2_out));  // open: bin, bout
  Multiplexer #(.width(8)) multiplexer_7 (.in0(subtractor_2_out), .in1(UINT), .out(multiplexer_7_out), .sel(ADD_V));
  or or_6 (or_6_out, and_6_out, ADD_V);
  Register #(.trigger("falling")) register_2 (
    .D(multiplexer_7_out), .en(or_6_out), .clk(CLK), .Q(register_2_q), .clr(in_2));
  dual_port_ram dual_port_ram_1 (
    .addr(RB_OUT), .pc(PC), .d(RA_OUT), .w(W_MEM), .clk(CLK), .instr(dual_port_ram_1_instr), .data(MEM_OUT));
  Comparator comparator_2 (.a(register_2_q), .b({8{1'b0}}), .eq(comparator_2_eq));  // open: gt, lt
  Multiplexer #(.width(8)) multiplexer_8 (
    .in0(dual_port_ram_1_instr), .in1(rom_1_data), .out(multiplexer_8_out), .sel(MICRO_CODE_EXECUTING));
  not not_3 (ADD_V_EXEC, comparator_2_eq);
  assign UINT = {{4{1'b0}}, multiplexer_8_out[3:0]};  // Bit_Extender bit_extender_2
  assign IMM = {{4{multiplexer_8_out[3]}}, multiplexer_8_out[3:0]};  // Bit_Extender bit_extender_3
  ROM #(.addrWidth(4), .dataWidth(13)) rom_2 (
    .addr(multiplexer_8_out[7:4]),
    .data({ADD_V, INC, LOAD_V, LOAD, BRZR, JI, ADDI, W_MEM, IMM_ULA, OP_ULA, W_RG}));
  Multiplexer #(.width(2)) multiplexer_9 (
    .in0(multiplexer_8_out[3:2]), .in1(2'b00), .out(multiplexer_9_out), .sel(ADDI));
  and and_7 (INC_ALL, ~multiplexer_8_out[2], ~multiplexer_8_out[3], INC);  // AND_Gate
  assign RB_IMM = {{6{1'b0}}, multiplexer_8_out[1:0]};  // Bit_Extender bit_extender_4
  banco_reg banco_reg_1 (
    .rb(multiplexer_8_out[1:0]), .rb_imm(RB_IMM), .CLK(CLK), .D(multiplexer_10_out), .inc_all(INC_ALL),
    .Reset(or_7_out), .ra(multiplexer_9_out), .WE(W_RG), .ADDV(ADD_V_EXEC), .Load(LOAD), .RA_OUT(RA_OUT),
    .RB_OUT(RB_OUT), .Y_OUT(y_out), .X_OUT(x_out));
  or or_7 (or_7_out, MANUAL_RESET_RG, in_2);
  Multiplexer #(.width(8)) multiplexer_10 (.in0(ULA_OUT), .in1(MEM_OUT), .out(multiplexer_10_out), .sel(LOAD));
  Multiplexer #(.width(8)) multiplexer_11 (.in0(PC), .in1(PC_2), .out(multiplexer_11_out), .sel(MICRO_CODE_EXECUTING));
  Multiplexer #(.width(8)) multiplexer_12 (.in0(RA_OUT), .in1(multiplexer_11_out), .out(multiplexer_12_out), .sel(JI));
  Multiplexer #(.width(8)) multiplexer_13 (.in0(RB_OUT), .in1(IMM), .out(multiplexer_13_out), .sel(IMM_ULA));
  Multiplexer #(.width(8)) multiplexer_14 (.in0(multiplexer_13_out), .in1(RB_IMM), .out(multiplexer_14_out), .sel(INC));
  Multiplexer #(.width(8)) multiplexer_15 (
    .in0(multiplexer_12_out), .in1(x_out), .out(multiplexer_15_out), .sel(and_8_out));
  Multiplexer #(.width(8)) multiplexer_16 (
    .in0(multiplexer_14_out), .in1(y_out), .out(multiplexer_16_out), .sel(and_8_out));
  not not_4 (not_4_out, JI);
  and and_8 (and_8_out, not_4_out, ADD_V_EXEC);
  ULA ula_1 (.op_ula(OP_ULA), .RA(multiplexer_15_out), .RB(multiplexer_16_out), .D(ULA_OUT), .ZERO(ZERO));

  // Other names for the same wires on the sheet: RESET = in_2

  // Notes on the sheet:
  //   JI (PC + IMM)
  //   RB (BRZR)
  //   contents of rom_1 (hex, n*v repeats v):
  //   40 38 c1 cb 1d 20 25 cc 3e 71 1b
  //   contents of rom_2 (hex, n*v repeats v):
  //   100 98 201 20 59 400 1000 809 1 3 5 7 9 b d f
endmodule

module banco_reg (
  input  Reset,
  input  CLK,
  input  ADDV,
  input  Load,
  input  [7:0] D,
  input  [1:0] ra,
  input  inc_all,
  input  [1:0] rb,
  input  [7:0] rb_imm,
  input  WE,
  output [7:0] X_OUT,
  output [7:0] Y_OUT,
  output [7:0] RA_OUT,
  output [7:0] RB_OUT
);

  wire and_1_out, and_2_out, demultiplexer_1_out0, demultiplexer_1_out1, demultiplexer_1_out2,
       demultiplexer_1_out3, demultiplexer_2_out0, demultiplexer_2_out1, not_1_out, or_1_out, or_2_out,
       or_3_out, or_4_out;
  wire [7:0] adder_1_out, adder_2_out, adder_3_out, adder_4_out, multiplexer_1_out, multiplexer_2_out,
       multiplexer_3_out, multiplexer_4_out, R0, R1, R2, R3;

  and and_1 (and_1_out, ADDV, Load);
  and and_2 (and_2_out, not_1_out, WE);
  Demultiplexer #(.select(2)) demultiplexer_1 (
    .out0(demultiplexer_1_out0), .out1(demultiplexer_1_out1), .out2(demultiplexer_1_out2),
    .out3(demultiplexer_1_out3), .in(and_2_out), .sel(ra));
  Demultiplexer #(.select(2)) demultiplexer_2 (
    .out0(demultiplexer_2_out0), .out1(demultiplexer_2_out1), .in(and_1_out), .sel(ra));  // open: out2, out3
  not not_1 (not_1_out, and_1_out);
  Register RX (.D(D), .en(demultiplexer_2_out0), .clk(CLK), .Q(X_OUT), .clr(Reset));
  Register RY (.D(D), .en(demultiplexer_2_out1), .clk(CLK), .Q(Y_OUT), .clr(Reset));
  or or_1 (or_1_out, demultiplexer_1_out0, inc_all);
  or or_2 (or_2_out, demultiplexer_1_out1, inc_all);
  or or_3 (or_3_out, demultiplexer_1_out2, inc_all);
  or or_4 (or_4_out, demultiplexer_1_out3, inc_all);
  Register u_R0 (.D(multiplexer_1_out), .en(or_1_out), .clk(CLK), .Q(R0), .clr(Reset));
  Register u_R1 (.D(multiplexer_2_out), .en(or_2_out), .clk(CLK), .Q(R1), .clr(Reset));
  Register u_R2 (.D(multiplexer_3_out), .en(or_3_out), .clk(CLK), .Q(R2), .clr(Reset));
  Register u_R3 (.D(multiplexer_4_out), .en(or_4_out), .clk(CLK), .Q(R3), .clr(Reset));
  Adder adder_1 (.a(rb_imm), .b(R0), .out(adder_1_out));  // open: cin, cout
  Adder adder_2 (.a(rb_imm), .b(R1), .out(adder_2_out));  // open: cin, cout
  Adder adder_3 (.a(rb_imm), .b(R2), .out(adder_3_out));  // open: cin, cout
  Adder adder_4 (.a(rb_imm), .b(R3), .out(adder_4_out));  // open: cin, cout
  Multiplexer #(.width(8)) multiplexer_1 (.in0(D), .in1(adder_1_out), .out(multiplexer_1_out), .sel(inc_all));
  Multiplexer #(.width(8)) multiplexer_2 (.in0(D), .in1(adder_2_out), .out(multiplexer_2_out), .sel(inc_all));
  Multiplexer #(.width(8)) multiplexer_3 (.in0(D), .in1(adder_3_out), .out(multiplexer_3_out), .sel(inc_all));
  Multiplexer #(.width(8)) multiplexer_4 (.in0(D), .in1(adder_4_out), .out(multiplexer_4_out), .sel(inc_all));
  Multiplexer #(.select(2), .width(8)) multiplexer_5 (.in0(R0), .in1(R1), .in2(R2), .in3(R3), .out(RA_OUT), .sel(ra));
  Multiplexer #(.select(2), .width(8)) multiplexer_6 (.in0(R0), .in1(R1), .in2(R2), .in3(R3), .out(RB_OUT), .sel(rb));

  // Other names for the same wires on the sheet: CLK_t = CLK; D_t[7:0] = D; R_t = Reset
endmodule

module ULA (
  input  [7:0] RA,
  input  [7:0] RB,
  input  [2:0] op_ula,
  output [7:0] D,
  output ZERO
);

  wire comparator_1_eq;
  wire [2:0] bit_extender_1_out;
  wire [7:0] adder_1_out, and_1_out, bit_extender_2_out, or_1_out, shifter_1_out, shifter_2_out,
       subtractor_1_out, xor_1_out;

  Bit_Extender #(.out_width(3)) bit_extender_1 (.in(RB), .out(bit_extender_1_out));
  assign and_1_out = RA & RB;  // AND_Gate and_1, 8 bits wide
  assign or_1_out = RA | RB;  // OR_Gate or_1, 8 bits wide
  Comparator comparator_1 (.a({8{1'b0}}), .b(RB), .eq(comparator_1_eq));  // open: gt, lt
  assign xor_1_out = RA ^ RB;  // XOR_Gate xor_1, 8 bits wide
  Adder adder_1 (.a(RA), .b(RB), .out(adder_1_out));  // open: cin, cout
  Subtractor subtractor_1 (.a(RA), .b(RB), .out(subtractor_1_out));  // open: bin, bout
  Shifter shifter_1 (.in(RA), .\dist (bit_extender_1_out), .out(shifter_1_out));
  Shifter #(.shift("lr")) shifter_2 (.in(RA), .\dist (bit_extender_1_out), .out(shifter_2_out));
  Comparator comparator_2 (.a(RA), .b({8{1'b0}}), .eq(ZERO));  // open: gt, lt
  assign bit_extender_2_out = {{7{1'b0}}, comparator_1_eq};  // Bit_Extender bit_extender_2
  Multiplexer #(.select(3), .width(8)) multiplexer_1 (
    .in0(bit_extender_2_out), .in1(and_1_out), .in2(or_1_out), .in3(xor_1_out), .in4(adder_1_out),
    .in5(subtractor_1_out), .in6(shifter_1_out), .in7(shifter_2_out), .out(D), .sel(op_ula));
endmodule

module branches (
  input  [31:0] rs1,
  input  [31:0] rs2,
  input  B,
  input  [1:0] B_in,
  output B_out
);

  wire comparator_1_eq, comparator_1_gt, comparator_1_lt, not_1_out, or_1_out;

  Comparator #(.width(32)) comparator_1 (
    .a(rs1), .b(rs2), .gt(comparator_1_gt), .eq(comparator_1_eq), .lt(comparator_1_lt));
  or or_1 (or_1_out, comparator_1_gt, comparator_1_eq);
  not not_1 (not_1_out, comparator_1_eq);
  Multiplexer #(.enable("true"), .select(2)) multiplexer_1 (
    .in0(comparator_1_eq), .in1(comparator_1_lt), .in2(not_1_out), .in3(or_1_out), .out(B_out), .sel(B_in),
    .en(B));
endmodule

module dual_port_ram (
  input  [7:0] addr,
  input  [7:0] pc,
  input  [7:0] d,
  input  w,
  input  clk,
  output [7:0] instr,
  output [7:0] data
);

  wire or_1_out;
  wire [7:0] multiplexer_1_out;

  or or_1 (or_1_out, w, clk);
  Multiplexer #(.width(8)) multiplexer_1 (.in0(addr), .in1(pc), .out(multiplexer_1_out), .sel(clk));
  RAM #(.asyncread("true")) ram_1 (.addr(multiplexer_1_out), .we(or_1_out), .oe(1'b1), .clk(clk), .din(d), .dout(data));
  Register #(.trigger("falling")) pcbuf (.D(data), .en(1'b1), .clk(clk), .Q(instr));  // open: clr
endmodule
