// Logisim project VLIW.circ as structural Verilog: 11 circuits, main circuit ProgramCounter
module ProgramCounter (
  input  [7:0] data,
  input  Clk,
  input  Reset,
  output [7:0] Pc_mais_1,
  output [7:0] Pc_out
);

  Register register_1 (.D(data), .en(1'b1), .clk(Clk), .Q(Pc_out), .clr(Reset));
  Adder adder_1 (.a(Pc_out), .b(8'h4), .out(Pc_mais_1));  // open: cin, cout
endmodule

module Main (
  input  in_1,
  input  MANUAL_RESET,
  input  in_3
);

  wire and_1_out, and_2_out, BOZI, BOZR, CLK, comparator_1_eq, comparator_1_gt, comparator_1_lt, JR, LD,
       MOVE, MOVH, MOVL, multiplexer_3_out, or_1_out, or_2_out, or_3_out, or_4_out, PR_OUT, R0_ZERO, RA_ZERO,
       ST, W_PR, WE_3, WE_4;
  wire [1:0] IMM_3, IMM_4, PR_OP;
  wire [2:0] OP_ULA_3, OP_ULA_4;
  wire [3:0] IMM_1, IMM_2;
  wire [7:0] LU_RESULT_1, LU_RESULT_2, LU_RESULT_3, LU_RESULT_4, MEM_OUT, multiplexer_1_out,
       multiplexer_2_out, multiplexer_4_out, PC, Pc_mais_1, R0_OUT, RA_1_OUT, RA_2_OUT, RA_3_OUT, RA_4_OUT,
       RB_1_OUT, RB_2_OUT, RB_3_OUT, RB_4_OUT;
  wire [7:2] rom_1_p4, rom_1_p5;
  wire [7:4] rom_1_p2, rom_1_p3;

  or or_1 (or_1_out, BOZR, JR);
  Multiplexer #(.width(8)) multiplexer_1 (.in0(LU_RESULT_2), .in1(RB_1_OUT), .out(multiplexer_1_out), .sel(or_1_out));
  and and_1 (and_1_out, R0_ZERO, BOZI);
  and and_2 (and_2_out, RA_ZERO, BOZR);
  or or_2 (or_2_out, and_1_out, JR, and_2_out);
  Multiplexer #(.width(8)) multiplexer_2 (
    .in0(Pc_mais_1), .in1(multiplexer_1_out), .out(multiplexer_2_out), .sel(or_2_out));
  or or_3 (or_3_out, in_3, MANUAL_RESET);
  Comparator comparator_1 (
    .a(RA_2_OUT), .b(RB_2_OUT), .gt(comparator_1_gt), .eq(comparator_1_eq), .lt(comparator_1_lt));
  Multiplexer #(.select(2)) multiplexer_3 (
    .in0(comparator_1_gt), .in1(comparator_1_eq), .in2(comparator_1_lt), .in3(1'b1), .out(multiplexer_3_out),
    .sel(PR_OP));
  Register #(.trigger("falling"), .width(1)) register_1 (
    .D(multiplexer_3_out), .en(W_PR), .clk(CLK), .Q(PR_OUT), .clr(in_3));
  ProgramCounter programcounter_1 (
    .data(multiplexer_2_out), .Clk(CLK), .Reset(or_3_out), .Pc_mais_1(Pc_mais_1), .Pc_out(PC));
  // ROM #(.line("quad")) rom_1: pin names not known; wires that end beside it: PC, {rom_1_p2, IMM_1}, {rom_1_p3, IMM_2}, {rom_1_p4, IMM_3}, {rom_1_p5, IMM_4}
  Clock clock_1 (.out(CLK));
  BRANCH_CONTROL branch_control_1 (
    .BIT_3(rom_1_p3[7]), .PR(PR_OUT), .BIT_0(rom_1_p3[4]), .BIT_1(rom_1_p3[5]), .BIT_2(rom_1_p3[6]),
    .PR_OP(PR_OP), .W_PR(W_PR), .BOZR(BOZR), .BOZI(BOZI), .JR(JR), .MOVE(MOVE));
  DATA_CONTROL data_control_1 (
    .BIT_1(rom_1_p2[5]), .BIT_2(rom_1_p2[6]), .BIT_3(rom_1_p2[7]), .PR(PR_OUT), .BIT_0(rom_1_p2[4]),
    .MOVH(MOVH), .MOVL(MOVL), .LD(LD), .ST(ST));
  Multiplexer #(.width(8)) multiplexer_4 (.in0(LU_RESULT_1), .in1(MEM_OUT), .out(multiplexer_4_out), .sel(LD));
  or or_4 (or_4_out, in_1, in_3);
  banco_reg banco_reg_1 (
    .WE_3(WE_3), .WE_4(WE_4), .MOVL(MOVL), .Reset(or_4_out), .CLK(CLK), .LD(LD), .MOVE(MOVE), .MOVH(MOVH),
    .RA_1(IMM_1[3:2]), .RA_2(IMM_2[3:2]), .RA_3(rom_1_p4[3:2]), .RA_4(rom_1_p5[3:2]), .RB_1(IMM_1[1:0]),
    .RB_2(IMM_2[1:0]), .RB_3(IMM_3), .RB_4(IMM_4), .DATA_1(multiplexer_4_out), .DATA_2(RB_2_OUT),
    .DATA_3(LU_RESULT_3), .DATA_4(LU_RESULT_4), .RA_1_OUT(RA_1_OUT), .RA_2_OUT(RA_2_OUT),
    .RA_3_OUT(RA_3_OUT), .RA_4_OUT(RA_4_OUT), .RO_OUT(R0_OUT), .RB_1_OUT(RB_1_OUT), .RB_2_OUT(RB_2_OUT),
    .RB_3_OUT(RB_3_OUT), .RB_4_OUT(RB_4_OUT));
  ARITHMETIC_CONTROL arithmetic_control_1 (
    .BIT_2(rom_1_p5[6]), .BIT_3(rom_1_p5[7]), .PR(PR_OUT), .BIT_0(rom_1_p5[4]), .BIT_1(rom_1_p5[5]),
    .OP_ULA_4_OUT(OP_ULA_4), .WE_4_OUT(WE_4));
  ARITHMETIC_CONTROL arithmetic_control_2 (
    .BIT_2(rom_1_p4[6]), .BIT_3(rom_1_p4[7]), .PR(PR_OUT), .BIT_0(rom_1_p4[4]), .BIT_1(rom_1_p4[5]),
    .OP_ULA_4_OUT(OP_ULA_3), .WE_4_OUT(WE_3));
  LU_DATA lu_data_1 (.MOVL(MOVL), .R0(R0_OUT), .IMM(IMM_1), .DATA(LU_RESULT_1));
  LU_BRANCH lu_branch_1 (
    .IMM(IMM_2), .RA(RA_2_OUT), .R0(R0_OUT), .PC(PC), .PC_PLUS_IMM(LU_RESULT_2), .RA_ZERO(RA_ZERO),
    .R0_ZERO(R0_ZERO));
  ULA ula_1 (.MULT_OPS(IMM_3), .op_ula(OP_ULA_3), .R0(R0_OUT), .RA(RA_3_OUT), .RB(RB_3_OUT), .D(LU_RESULT_3));
  ULA ula_2 (.MULT_OPS(IMM_4), .op_ula(OP_ULA_4), .R0(R0_OUT), .RA(RA_4_OUT), .RB(RB_4_OUT), .D(LU_RESULT_4));
  RAM #(.asyncread("true")) ram_1 (.addr(RB_1_OUT), .we(ST), .oe(1'b1), .clk(CLK), .din(RA_1_OUT), .dout(MEM_OUT));

  // Other names for the same wires on the sheet: RESET = in_3

  // Notes on the sheet:
  //   contents of rom_1 (hex, n*v repeats v):
  //   f0 b0 f0 f0 2f f0 15 1a 3f f0 f0 1f 34 f0 f0 4 f0 f0 1d 18 19 f0 f0 f0 26 f0 f0 15 20 f0 f0 4 31 f0
  //   f0 6 f0 f0 17 1b 19 f0 17 1b 19 f0 17 1b 19 f0 17 1b 19 f0 42 f0 f0 1b f0 f0 2f f0 f0 f0 3f f0 f0 f0
  //   8 f0 f0 f0 21 f0 f0 6 33 f0 f0 6 20 f0 f0 c 30 f0 f0 e f0 f0 f0 40 f0 f0 1c 14 1d f0 18 4*f0 42 f0
  //   1c f0 f0 28 f0 f0 1f 3c f0 f0 f0 2f f0 f0 c 3e f0 f0 f0 1c f0 f0 f0 3f f0 f0 f0 8 f0 f0 f0 3d f0 f0
  //   f0 18 f0 f0 f0 3f f0 f0 f0 8 5*f0 4 f0 1 f0 f0 6 d f0 f0 6 2f f0 f0 c 1d f0 f0 16 3f f0 f0 16 f0 f0
  //   f0 4 1 f0 f0 6 d f0 f0 6 2f f0 f0 c 1d f0 f0 16 3f f0 f0 16 f0 f0 f0 4 1 f0 f0 6 d f0 f0 6 2f f0 f0
  //   c 1d f0 f0 16 3e f0 f0 16 c f0 f0 f0 3d f0 f0 f0 8 6*f0 8 18 f0 f0 42 2f 3 5*f0 10 f0 10 f0 f0
endmodule

module banco_reg (
  input  Reset,
  input  CLK,
  input  LD,
  input  WE_3,
  input  MOVE,
  input  WE_4,
  input  MOVH,
  input  MOVL,
  input  [1:0] RA_1,
  input  [1:0] RA_2,
  input  [1:0] RA_3,
  input  [1:0] RA_4,
  input  [1:0] RB_1,
  input  [1:0] RB_2,
  input  [1:0] RB_3,
  input  [1:0] RB_4,
  input  [7:0] DATA_1,
  input  [7:0] DATA_2,
  input  [7:0] DATA_3,
  input  [7:0] DATA_4,
  output [7:0] RA_1_OUT,
  output [7:0] RB_1_OUT,
  output [7:0] RA_2_OUT,
  output [7:0] RB_2_OUT,
  output [7:0] RA_3_OUT,
  output [7:0] RB_3_OUT,
  output [7:0] RA_4_OUT,
  output [7:0] RB_4_OUT,
  output [7:0] RO_OUT
);

  wire demultiplexer_1_out0, or_1_out, or_2_out, or_3_out, or_4_out, or_10_out, W_R0_1, W_R0_2, W_R0_3,
       W_R0_4, W_R1_1, W_R1_2, W_R1_3, W_R1_4, W_R2_1, W_R2_2, W_R2_3, W_R2_4, W_R3_1, W_R3_2, W_R3_3, W_R3_4;
  wire [7:0] D_R0_1, D_R0_2, D_R0_3, D_R0_4, D_R1_1, D_R1_2, D_R1_3, D_R1_4, D_R2_1, D_R2_2, D_R2_3, D_R2_4,
       D_R3_1, D_R3_2, D_R3_3, D_R3_4, demultiplexer_5_out0, multiplexer_1_out, multiplexer_2_out, or_6_out,
       or_7_out, or_8_out, or_9_out, R1, R2, R3;

  Demultiplexer #(.select(2)) demultiplexer_1 (
    .out0(demultiplexer_1_out0), .out1(W_R1_1), .out2(W_R2_1), .out3(W_R3_1), .in(LD), .sel(RA_1));
  Demultiplexer #(.select(2)) demultiplexer_2 (
    .out0(W_R0_2), .out1(W_R1_2), .out2(W_R2_2), .out3(W_R3_2), .in(MOVE), .sel(RA_2));
  Demultiplexer #(.select(2)) demultiplexer_3 (
    .out0(W_R0_3), .out1(W_R1_3), .out2(W_R2_3), .out3(W_R3_3), .in(WE_3), .sel(RA_3));
  Demultiplexer #(.select(2)) demultiplexer_4 (
    .out0(W_R0_4), .out1(W_R1_4), .out2(W_R2_4), .out3(W_R3_4), .in(WE_4), .sel(RA_4));
  or or_1 (or_1_out, W_R0_1, W_R0_2, W_R0_3, W_R0_4);
  or or_2 (or_2_out, W_R1_1, W_R1_3, W_R1_2, W_R1_4);
  or or_3 (or_3_out, W_R2_1, W_R2_2, W_R2_3, W_R2_4);
  or or_4 (or_4_out, W_R3_1, W_R3_2, W_R3_3, W_R3_4);
  or or_5 (W_R0_1, MOVH, MOVL, demultiplexer_1_out0);
  assign or_6_out = D_R0_1 | D_R0_2 | D_R0_3 | D_R0_4;  // OR_Gate or_6, 8 bits wide
  Register R0 (.D(or_6_out), .en(or_1_out), .clk(CLK), .Q(RO_OUT), .clr(Reset));
  assign or_7_out = D_R1_1 | D_R1_2 | D_R1_3 | D_R1_4;  // OR_Gate or_7, 8 bits wide
  Register u_R1 (.D(or_7_out), .en(or_2_out), .clk(CLK), .Q(R1), .clr(Reset));
  assign or_8_out = D_R2_1 | D_R2_2 | D_R2_3 | D_R2_4;  // OR_Gate or_8, 8 bits wide
  Register u_R2 (.D(or_8_out), .en(or_3_out), .clk(CLK), .Q(R2), .clr(Reset));
  assign or_9_out = D_R3_1 | D_R3_2 | D_R3_3 | D_R3_4;  // OR_Gate or_9, 8 bits wide
  Register u_R3 (.D(or_9_out), .en(or_4_out), .clk(CLK), .Q(R3), .clr(Reset));
  Multiplexer #(.width(8)) multiplexer_1 (.in0({8{1'b0}}), .in1(DATA_1), .out(multiplexer_1_out), .sel(LD));
  Multiplexer #(.width(8)) multiplexer_2 (.in0({8{1'b0}}), .in1(DATA_2), .out(multiplexer_2_out), .sel(MOVE));
  Demultiplexer #(.select(2), .width(8)) demultiplexer_5 (
    .out0(demultiplexer_5_out0), .out1(D_R1_1), .out2(D_R2_1), .out3(D_R3_1), .in(multiplexer_1_out),
    .sel(RA_1));
  Demultiplexer #(.select(2), .width(8)) demultiplexer_6 (
    .out0(D_R0_2), .out1(D_R1_2), .out2(D_R2_2), .out3(D_R3_2), .in(multiplexer_2_out), .sel(RA_2));
  Demultiplexer #(.select(2), .width(8)) demultiplexer_7 (
    .out0(D_R0_3), .out1(D_R1_3), .out2(D_R2_3), .out3(D_R3_3), .in(DATA_3), .sel(RA_3));
  Demultiplexer #(.select(2), .width(8)) demultiplexer_8 (
    .out0(D_R0_4), .out1(D_R1_4), .out2(D_R2_4), .out3(D_R3_4), .in(DATA_4), .sel(RA_4));
  Multiplexer #(.select(2), .width(8)) multiplexer_3 (
    .in0(RO_OUT), .in1(R1), .in2(R2), .in3(R3), .out(RA_1_OUT), .sel(RA_1));
  Multiplexer #(.select(2), .width(8)) multiplexer_4 (
    .in0(RO_OUT), .in1(R1), .in2(R2), .in3(R3), .out(RA_2_OUT), .sel(RA_2));
  Multiplexer #(.select(2), .width(8)) multiplexer_5 (
    .in0(RO_OUT), .in1(R1), .in2(R2), .in3(R3), .out(RA_3_OUT), .sel(RA_3));
  Multiplexer #(.select(2), .width(8)) multiplexer_6 (
    .in0(RO_OUT), .in1(R1), .in2(R2), .in3(R3), .out(RA_4_OUT), .sel(RA_4));
  Multiplexer #(.select(2), .width(8)) multiplexer_7 (
    .in0(RO_OUT), .in1(R1), .in2(R2), .in3(R3), .out(RB_1_OUT), .sel(RB_1));
  Multiplexer #(.select(2), .width(8)) multiplexer_8 (
    .in0(RO_OUT), .in1(R1), .in2(R2), .in3(R3), .out(RB_2_OUT), .sel(RB_2));
  Multiplexer #(.select(2), .width(8)) multiplexer_9 (
    .in0(RO_OUT), .in1(R1), .in2(R2), .in3(R3), .out(RB_3_OUT), .sel(RB_3));
  Multiplexer #(.select(2), .width(8)) multiplexer_10 (
    .in0(RO_OUT), .in1(R1), .in2(R2), .in3(R3), .out(RB_4_OUT), .sel(RB_4));
  or or_10 (or_10_out, MOVL, MOVH);
  Multiplexer #(.width(8)) multiplexer_11 (.in0(demultiplexer_5_out0), .in1(DATA_1), .out(D_R0_1), .sel(or_10_out));

  // Other names for the same wires on the sheet: CLK_t = CLK; R0[7:0] = RO_OUT; R_t = Reset
endmodule

module ULA (
  input  [1:0] MULT_OPS,
  input  [7:0] R0,
  input  [7:0] RA,
  input  [7:0] RB,
  input  [2:0] op_ula,
  output [7:0] D
);

  wire comparator_1_eq, or_1_out;
  wire [7:0] adder_1_out, and_1_out, bit_extender_1_out, multiplexer_1_out, multiplexer_2_out,
       multiplexer_3_out, not_1_out, or_2_out, shifter_1_out, shifter_2_out, subtractor_1_out, xnor_1_out,
       xor_1_out;

  or or_1 (or_1_out, RB[7], RB[6], RB[5], RB[4], RB[3]);
  Adder adder_1 (.a(RA), .b(RB), .out(adder_1_out));  // open: cin, cout
  Subtractor subtractor_1 (.a(RA), .b(RB), .out(subtractor_1_out));  // open: bin, bout
  assign or_2_out = RA | RB;  // OR_Gate or_2, 8 bits wide
  Comparator comparator_1 (.a({8{1'b0}}), .b(RB), .eq(comparator_1_eq));  // open: gt, lt
  Shifter shifter_1 (.in(RA), .\dist (RB[2:0]), .out(shifter_1_out));
  Multiplexer #(.width(8)) multiplexer_1 (
    .in0(shifter_1_out), .in1({8{1'b0}}), .out(multiplexer_1_out), .sel(or_1_out));
  Shifter #(.shift("lr")) shifter_2 (.in(RA), .\dist (RB[2:0]), .out(shifter_2_out));
  Multiplexer #(.width(8)) multiplexer_2 (
    .in0(shifter_2_out), .in1({8{1'b0}}), .out(multiplexer_2_out), .sel(or_1_out));
  assign not_1_out = ~RA;  // NOT_Gate not_1, 8 bits wide
  assign xor_1_out = R0 ^ RA;  // XOR_Gate xor_1, 8 bits wide
  assign and_1_out = R0 & RA;  // AND_Gate and_1, 8 bits wide
  assign xnor_1_out = ~(R0 ^ RA);  // XNOR_Gate xnor_1, 8 bits wide
  assign bit_extender_1_out = {{7{1'b0}}, comparator_1_eq};  // Bit_Extender bit_extender_1
  Multiplexer #(.select(2), .width(8)) multiplexer_3 (
    .in0(not_1_out), .in1(xor_1_out), .in2(and_1_out), .in3(xnor_1_out), .out(multiplexer_3_out),
    .sel(MULT_OPS));
  Multiplexer #(.select(3), .width(8)) multiplexer_4 (
    .in0(adder_1_out), .in1(subtractor_1_out), .in2(multiplexer_3_out), .in3(or_2_out),
    .in4(bit_extender_1_out), .in5(multiplexer_1_out), .in6(multiplexer_2_out), .in7({8{1'b0}}), .out(D),
    .sel(op_ula));
endmodule

module branches (
  input  [31:0] rs1,
  input  [31:0] rs2,
  input  B,
  input  [1:0] B_in,
  output B_out
);

  wire comparator_1_eq, comparator_1_gt, comparator_1_lt, not_1_out, or_1_out;

  Comparator #(.width(32)) comparator_1 (
    .a(rs1), .b(rs2), .gt(comparator_1_gt), .eq(comparator_1_eq), .lt(comparator_1_lt));
  or or_1 (or_1_out, comparator_1_gt, comparator_1_eq);
  not not_1 (not_1_out, comparator_1_eq);
  Multiplexer #(.enable("true"), .select(2)) multiplexer_1 (
    .in0(comparator_1_eq), .in1(comparator_1_lt), .in2(not_1_out), .in3(or_1_out), .out(B_out), .sel(B_in),
    .en(B));
endmodule

module dual_port_ram (
  input  [7:0] addr,
  input  [7:0] pc,
  input  [7:0] d,
  input  w,
  output [7:0] instr,
  output [7:0] data
);

  wire clock_1_out, or_1_out;
  wire [7:0] multiplexer_1_out;

  Clock clock_1 (.out(clock_1_out));
  or or_1 (or_1_out, w, clock_1_out);
  Multiplexer #(.width(8)) multiplexer_1 (.in0(addr), .in1(pc), .out(multiplexer_1_out), .sel(clock_1_out));
  RAM #(.asyncread("true")) ram_1 (
    .addr(multiplexer_1_out), .we(or_1_out), .oe(1'b1), .clk(clock_1_out), .din(d), .dout(data));
  Register #(.trigger("falling")) pcbuf (.D(data), .en(1'b1), .clk(clock_1_out), .Q(instr));  // open: clr
endmodule

module LU_BRANCH (
  input  [7:0] RA,
  input  [7:0] R0,
  input  [7:0] PC,
  input  [3:0] IMM,
  output RA_ZERO,
  output R0_ZERO,
  output [7:0] PC_PLUS_IMM
);

  wire [7:0] bit_extender_1_out, multiplier_1_out;

  Comparator comparator_1 (.a(RA), .b({8{1'b0}}), .eq(RA_ZERO));  // open: gt, lt
  Comparator comparator_2 (.a(R0), .b({8{1'b0}}), .eq(R0_ZERO));  // open: gt, lt
  assign bit_extender_1_out = {{4{IMM[3]}}, IMM};  // Bit_Extender bit_extender_1
  Multiplier multiplier_1 (.a(bit_extender_1_out), .b(8'h4), .out(multiplier_1_out));  // open: cin, cout
  Adder adder_1 (.a(PC), .b(multiplier_1_out), .out(PC_PLUS_IMM));  // open: cin, cout
endmodule

module LU_DATA (
  input  [3:0] IMM,
  input  MOVL,
  input  [7:0] R0,
  output [7:0] DATA
);

  wire [7:0] adder_1_out, adder_2_out, bit_extender_1_out, bit_extender_2_out, bit_extender_3_out,
       shifter_1_out, shifter_2_out;

  assign bit_extender_1_out = {{4{1'b0}}, R0[3:0]};  // Bit_Extender bit_extender_1
  assign bit_extender_2_out = {{4{1'b0}}, R0[7:4]};  // Bit_Extender bit_extender_2
  assign bit_extender_3_out = {{4{1'b0}}, IMM};  // Bit_Extender bit_extender_3
  Shifter shifter_1 (.in(bit_extender_3_out), .\dist (3'b100), .out(shifter_1_out));
  Shifter shifter_2 (.in(bit_extender_2_out), .\dist (3'b100), .out(shifter_2_out));
  Adder adder_1 (.a(bit_extender_1_out), .b(shifter_1_out), .out(adder_1_out));  // open: cin, cout
  Adder adder_2 (.a(bit_extender_3_out), .b(shifter_2_out), .out(adder_2_out));  // open: cin, cout
  Multiplexer #(.width(8)) multiplexer_1 (.in0(adder_1_out), .in1(adder_2_out), .out(DATA), .sel(MOVL));
endmodule

module ARITHMETIC_CONTROL (
  input  PR,
  input  BIT_0,
  input  BIT_1,
  input  BIT_2,
  input  BIT_3,
  output [2:0] OP_ULA_4_OUT,
  output WE_4_OUT
);

  wire and_1_out, and_2_out, and_3_out, and_4_out, and_5_out, NOT_PR, or_1_out, TRUE, WE;

  not not_1 (NOT_PR, PR);
  not not_2 (TRUE, BIT_3);
  and and_1 (and_1_out, BIT_0, BIT_1, BIT_2, BIT_3);
  not not_3 (WE, and_1_out);
  and and_2 (and_2_out, TRUE, PR);
  and and_3 (and_3_out, BIT_3, NOT_PR);
  or or_1 (or_1_out, and_2_out, and_3_out);
  Multiplexer #(.width(3)) multiplexer_1 (
    .in0(3'b111), .in1({BIT_2, BIT_1, BIT_0}), .out(OP_ULA_4_OUT), .sel(or_1_out));
  and and_4 (and_4_out, NOT_PR, BIT_3, WE);
  and and_5 (and_5_out, PR, TRUE, WE);
  or or_2 (WE_4_OUT, and_4_out, and_5_out);

  // Other names for the same wires on the sheet: NOT_TRUE = BIT_3; OP_ULA[2:0] = {BIT_2, BIT_1, BIT_0}
endmodule

module DATA_CONTROL (
  input  PR,
  input  BIT_0,
  input  BIT_1,
  input  BIT_2,
  input  BIT_3,
  output LD,
  output ST,
  output MOVH,
  output MOVL
);

  wire and_1_out, and_2_out, and_3_out, and_4_out, and_5_out, and_6_out, and_7_out, HIT, not_5_out,
       NOT_BIT_0, NOT_BIT_1, NOT_PR, TRUE;

  not not_1 (TRUE, BIT_2);
  not not_2 (NOT_PR, PR);
  not not_3 (NOT_BIT_0, BIT_0);
  not not_4 (NOT_BIT_1, BIT_1);
  and and_1 (and_1_out, BIT_0, BIT_1, BIT_2, BIT_3);
  not not_5 (not_5_out, and_1_out);
  and and_2 (and_2_out, TRUE, PR);
  and and_3 (and_3_out, BIT_2, NOT_PR);
  and and_4 (and_4_out, NOT_BIT_0, NOT_BIT_1);
  and and_5 (and_5_out, BIT_0, NOT_BIT_1);
  and and_6 (and_6_out, NOT_BIT_0, BIT_1);
  and and_7 (and_7_out, BIT_0, not_5_out, BIT_1);
  or or_1 (HIT, and_2_out, and_3_out);
  and and_8 (LD, HIT, and_4_out);
  and and_9 (ST, HIT, and_5_out);
  and and_10 (MOVH, HIT, and_6_out);
  and and_11 (MOVL, HIT, and_7_out);

  // Other names for the same wires on the sheet: NOT_TRUE = BIT_2
endmodule

module BRANCH_CONTROL (
  input  PR,
  input  BIT_0,
  input  BIT_1,
  input  BIT_2,
  input  BIT_3,
  output BOZR,
  output BOZI,
  output JR,
  output MOVE,
  output [1:0] PR_OP,
  output W_PR
);

  wire and_2_out, and_3_out, and_4_out, and_5_out, and_6_out, and_7_out, HIT, NOP, NOT_BIT_0, NOT_BIT_1,
       NOT_BIT_3, NOT_NOP, NOT_PR, TRUE;

  not not_1 (TRUE, BIT_2);
  not not_2 (NOT_PR, PR);
  not not_3 (NOT_BIT_0, BIT_0);
  not not_4 (NOT_BIT_1, BIT_1);
  not not_5 (NOT_BIT_3, BIT_3);
  and and_1 (NOP, BIT_0, BIT_1, BIT_2, BIT_3);
  not not_6 (NOT_NOP, NOP);
  and and_2 (and_2_out, TRUE, PR);
  and and_3 (and_3_out, BIT_2, NOT_PR);
  and and_4 (and_4_out, NOT_BIT_0, NOT_BIT_3, NOT_BIT_1);
  and and_5 (and_5_out, BIT_0, NOT_BIT_3, NOT_BIT_1);
  and and_6 (and_6_out, NOT_BIT_0, NOT_BIT_3, BIT_1);
  and and_7 (and_7_out, BIT_0, NOT_BIT_3, BIT_1);
  and and_8 (W_PR, NOT_NOP, BIT_3);
  or or_1 (HIT, and_2_out, and_3_out);
  and and_9 (BOZR, HIT, and_4_out);
  and and_10 (BOZI, HIT, and_5_out);
  and and_11 (JR, HIT, and_6_out);
  and and_12 (MOVE, HIT, and_7_out);

  assign PR_OP = {BIT_1, BIT_0};

  // Other names for the same wires on the sheet: NOT_TRUE = BIT_2
endmodule
