// Logisim project Vetorial.circ as structural Verilog: 25 circuits, main circuit ProgramCounter
module ProgramCounter (
  input  [7:0] data,
  input  WE_IF,
  input  Clk,
  input  Reset,
  output [7:0] Pc_mais_1,
  output [7:0] Pc_out
);

  Register register_1 (.D(data), .en(WE_IF), .clk(Clk), .Q(Pc_out), .clr(Reset));
  Adder adder_1 (.a(Pc_out), .b(8'h1), .out(Pc_mais_1));  // open: cin, cout
endmodule

module Main (
  input  in_1,
  input  MANUAL_RESET,
  input  in_3,
  input  in_4,
  input  in_5,
  input  in_6,
  input  in_7
);

  wire and_1_out, and_2_out, BRANCH, BRZR, CLK, comparator_1_eq, comparator_3_eq, LD, LD_EX, LD_MEM, LD_WB,
       LOOP_AGAIN, LOOPING, MOV, nop, or_1_out, or_2_out, or_4_out, or_5_out, or_6_out, or_7_out, or_8_out,
       REP, REP_OR_LOOP, ST_SR, ST_SR_EX, ST_SR_MEM, ST_V, ST_V_EX, ST_V_MEM, WE_IF, WE_SR, WE_SR_EX,
       WE_SR_MEM, WE_SR_WB, WE_V, WE_V_EX, WE_V_MEM, WE_V_WB;
  wire [1:0] F_BR, F_R1, F_RA, F_RA_REP, F_RB, F_RB_REP, F_V_R1, F_V_RA, F_V_RB, INC_OPS_EX, RA_EX, RB_EX,
       RD, RD_EX, RD_MEM, RD_WB;
  wire [2:0] OP_ULA, OP_ULA_EX, OP_V_ULA_EX;
  wire [3:0] IMM, IMM_EX, IMM_V_EX, OPCODE;
  wire [7:0] ADDRESS_q, COUNTER_q, DATA_V0_WB, DATA_V1_WB, DATA_V2_WB, DATA_V3_WB, DATA_WB, MEM_OUT_0,
       MEM_OUT_1, MEM_OUT_2, MEM_OUT_3, MEM_OUT_SR, MEM_OUT_SR_WB, MEM_V0_WB, MEM_V1_WB, MEM_V2_WB,
       MEM_V3_WB, multiplexer_3_out, multiplexer_4_out, multiplexer_5_out, multiplexer_6_out,
       multiplexer_7_out, multiplexer_9_out, NUM_OF_INSTRUCTIONS_q, PC, PC_BRANCH, PC_MAIS_1, R1_0_OUT,
       R1_0_OUT_EX, R1_1_OUT, R1_1_OUT_EX, R1_2_OUT, R1_2_OUT_EX, R1_3_OUT, R1_3_OUT_EX, R1_OUT_SR,
       R1_OUT_SR_EX, R1_ULA, R1_V0_ULA, R1_V1_ULA, R1_V2_ULA, R1_V3_ULA, RA_0_OUT, RA_0_OUT_EX, RA_1_OUT,
       RA_1_OUT_EX, RA_2_OUT, RA_2_OUT_EX, RA_3_OUT, RA_3_OUT_EX, RA_OUT_SR, RA_OUT_SR_EX, RA_OUT_SR_MEM,
       RA_REP, RA_ULA, RA_V0_MEM, RA_V0_ULA, RA_V1_MEM, RA_V1_ULA, RA_V2_MEM, RA_V2_ULA, RA_V3_MEM,
       RA_V3_ULA, RB_0_OUT, RB_0_OUT_EX, RB_1_OUT, RB_1_OUT_EX, RB_2_OUT, RB_2_OUT_EX, RB_3_OUT, RB_3_OUT_EX,
       RB_OUT_SR, RB_OUT_SR_EX, RB_OUT_SR_MEM, RB_REP, RB_ULA, RB_V0_MEM, RB_V0_ULA, RB_V1_MEM, RB_V1_ULA,
       RB_V2_MEM, RB_V2_ULA, RB_V3_MEM, RB_V3_ULA, rom_1_data, subtractor_1_out, subtractor_2_out,
       subtractor_3_out, TIMES_q, ULA_RESULT_0, ULA_RESULT_0_MEM, ULA_RESULT_0_WB, ULA_RESULT_1,
       ULA_RESULT_1_MEM, ULA_RESULT_1_WB, ULA_RESULT_2, ULA_RESULT_2_MEM, ULA_RESULT_2_WB, ULA_RESULT_3,
       ULA_RESULT_3_MEM, ULA_RESULT_3_WB, ULA_RESULT_SR, ULA_RESULT_SR_MEM, ULA_RESULT_SR_WB;

  Register ADDRESS (.D(PC), .en(REP), .clk(CLK), .Q(ADDRESS_q), .clr(in_3));
  Multiplexer #(.select(2), .width(8)) multiplexer_1 (
    .in0(RA_OUT_SR), .in1(DATA_WB), .in2(ULA_RESULT_SR_MEM), .in3(ULA_RESULT_SR), .out(RA_REP), .sel(F_RA_REP));
  Multiplexer #(.select(2), .width(8)) multiplexer_2 (
    .in0(RB_OUT_SR), .in1(DATA_WB), .in2(ULA_RESULT_SR_MEM), .in3(ULA_RESULT_SR), .out(RB_REP), .sel(F_RB_REP));
  Register NUM_OF_INSTRUCTIONS (.D(RB_REP), .en(REP), .clk(CLK), .Q(NUM_OF_INSTRUCTIONS_q), .clr(in_3));
  Subtractor subtractor_1 (.a(TIMES_q), .b(8'h1), .out(subtractor_1_out));  // open: bin, bout
  Multiplexer #(.width(8)) multiplexer_3 (.in0(PC_MAIS_1), .in1(PC_BRANCH), .out(multiplexer_3_out), .sel(BRZR));
  Subtractor subtractor_2 (.a(COUNTER_q), .b(8'h1), .out(subtractor_2_out));  // open: bin, bout
  and and_1 (and_1_out, LOOP_AGAIN, LOOPING);
  Multiplexer #(.width(8)) multiplexer_4 (
    .in0(multiplexer_3_out), .in1(ADDRESS_q), .out(multiplexer_4_out), .sel(and_1_out));
  or or_1 (or_1_out, in_3, MANUAL_RESET);
  Multiplexer #(.width(8)) multiplexer_5 (
    .in0(subtractor_2_out), .in1(NUM_OF_INSTRUCTIONS_q), .out(multiplexer_5_out), .sel(REP_OR_LOOP));
  Multiplexer #(.width(8)) multiplexer_6 (.in0(subtractor_1_out), .in1(RA_REP), .out(multiplexer_6_out), .sel(REP));
  FOW_UNIT_REP fow_unit_rep_1 (
    .RD_EX(RD_EX), .RD_MEM(RD_MEM), .RA(RD), .RB(IMM[1:0]), .WE_EX(WE_SR_EX), .WE_MEM(WE_SR_MEM),
    .WE_WB(WE_SR_WB), .RD_WB(RD_WB), .FOW_A(F_RA_REP), .FOW_B(F_RB_REP));
  Register TIMES (.D(multiplexer_6_out), .en(REP_OR_LOOP), .clk(CLK), .Q(TIMES_q), .clr(in_3));
  ProgramCounter programcounter_1 (
    .data(multiplexer_4_out), .Clk(CLK), .WE_IF(WE_IF), .Reset(or_1_out), .Pc_mais_1(PC_MAIS_1), .Pc_out(PC));
  Multiplexer #(.width(8)) multiplexer_7 (
    .in0(multiplexer_5_out), .in1(subtractor_3_out), .out(multiplexer_7_out), .sel(REP));
  Subtractor subtractor_3 (.a(RB_REP), .b(8'h1), .out(subtractor_3_out));  // open: bin, bout
  Register COUNTER (.D(multiplexer_7_out), .en(or_2_out), .clk(CLK), .Q(COUNTER_q), .clr(in_3));
  or or_2 (or_2_out, REP, LOOPING);
  and and_2 (and_2_out, LOOPING, LOOP_AGAIN);
  Comparator comparator_1 (.a(TIMES_q), .b({8{1'b0}}), .eq(comparator_1_eq));  // open: gt, lt
  ROM rom_1 (.addr(PC), .data(rom_1_data));
  not not_1 (LOOPING, comparator_1_eq);
  or or_3 (REP_OR_LOOP, REP, and_2_out);
  Clock clock_1 (.out(CLK));
  Comparator comparator_2 (.a(COUNTER_q), .b(8'h1), .eq(LOOP_AGAIN));  // open: gt, lt
  IF_ID if_id_1 (
    .INSTRUCTION_IN(rom_1_data), .NOP(nop), .clk(CLK), .WE(WE_IF), .RESET(in_3),
    .INSTRUCTION_OUT({OPCODE, IMM}));
  Multiplexer #(.width(2)) multiplexer_8 (.in0(IMM[3:2]), .in1(2'b01), .out(RD), .sel(MOV));
  ROM #(.addrWidth(4), .dataWidth(11)) rom_2 (
    .addr(OPCODE), .data({ST_SR, ST_V, WE_SR, WE_V, MOV, REP, BRANCH, LD, OP_ULA}));
  HAZARD_UNIT hazard_unit_1 (
    .RD_ex(RD_EX), .RA_id(RD), .RB_id(IMM[1:0]), .LD_EX(LD_EX), .BRZR(BRZR), .nop(nop), .WE_IF(WE_IF));
  FOW_UNIT_BRANCH fow_unit_branch_1 (
    .RD_EX(RD_EX), .RA_ID(RD), .RD_MEM(RD_MEM), .WE_EX(WE_SR_EX), .WE_MEM(WE_SR_WB), .Forw_Br(F_BR));
  or or_4 (or_4_out, in_4, in_3);
  or or_5 (or_5_out, in_5, in_3);
  or or_6 (or_6_out, in_6, in_3);
  or or_7 (or_7_out, in_7, in_3);
  Multiplexer #(.select(2), .width(8)) multiplexer_9 (
    .in0(RA_OUT_SR), .in1(RA_OUT_SR_MEM), .in2(ULA_RESULT_SR), .out(multiplexer_9_out), .sel(F_BR));  // open: in3
  REG_BANK_VET_0 reg_bank_vet_0_1 (
    .WE(WE_V_WB), .Reset(or_4_out), .CLK(CLK), .RA(RD), .RD(RD_WB), .RB(IMM[1:0]), .DATA(DATA_V0_WB),
    .RA_OUT(RA_0_OUT), .RB_OUT(RB_0_OUT), .R1_OUT(R1_0_OUT));
  REG_BANK_VET_1 reg_bank_vet_1_1 (
    .WE(WE_V_WB), .Reset(or_5_out), .CLK(CLK), .RA(RD), .RD(RD_WB), .RB(IMM[1:0]), .DATA(DATA_V1_WB),
    .RA_OUT(RA_1_OUT), .RB_OUT(RB_1_OUT), .R1_OUT(R1_1_OUT));
  REG_BANK_VET_2 reg_bank_vet_2_1 (
    .WE(WE_V_WB), .DATA(DATA_V2_WB), .Reset(or_6_out), .CLK(CLK), .RB(IMM[1:0]), .RA(RD), .RD(RD_WB),
    .RA_OUT(RA_2_OUT), .RB_OUT(RB_2_OUT), .R1_OUT(R1_2_OUT));
  REG_BANK_VET_3 reg_bank_vet_3_1 (
    .WE(WE_V_WB), .Reset(or_7_out), .CLK(CLK), .RA(RD), .RD(RD_WB), .RB(IMM[1:0]), .DATA(DATA_V3_WB),
    .RA_OUT(RA_3_OUT), .RB_OUT(RB_3_OUT), .R1_OUT(R1_3_OUT));
  Comparator comparator_3 (.a(multiplexer_9_out), .b({8{1'b0}}), .eq(comparator_3_eq));  // open: gt, lt
  or or_8 (or_8_out, in_1, in_3);
  BRANCH_PC branch_pc_1 (
    .RD_MEM(RD_MEM), .RB_ID(IMM[1:0]), .WE_MEM(WE_SR_MEM), .RB_OUT(RB_OUT_SR), .ULA_RESULT(ULA_RESULT_SR),
    .PC_BRANCH(PC_BRANCH));
  and and_3 (BRZR, BRANCH, comparator_3_eq);
  banco_reg banco_reg_1 (
    .WE(WE_SR_WB), .DATA(DATA_WB), .Reset(or_8_out), .CLK(CLK), .RD(RD_WB), .RB(IMM[1:0]), .RA(RD),
    .RA_OUT(RA_OUT_SR), .RB_OUT(RB_OUT_SR), .R1_OUT(R1_OUT_SR));
  ID_EX id_ex_1 (
    .NOP(nop), .RESET(in_3), .CLK(CLK), .LD(LD), .WE_SR(WE_SR), .ST_SR(ST_SR), .OP_ULA(OP_ULA),
    .R1_IN(R1_OUT_SR), .IMM(IMM), .RA_ID(RD), .INC_OPS(IMM[1:0]), .RA_SR(RA_OUT_SR), .RB_SR(RB_OUT_SR),
    .RB_ID(IMM[1:0]), .RD_ID(RD), .R1_OUT(R1_OUT_SR_EX), .IMM_OUT(IMM_EX), .RA_OUT(RA_EX), .RB_OUT(RB_EX),
    .RD_OUT(RD_EX), .INC_OPS_OUT(INC_OPS_EX), .OP_ULA_OUT(OP_ULA_EX), .RA_SR_OUT(RA_OUT_SR_EX),
    .RB_SR_OUT(RB_OUT_SR_EX), .LD_OUT(LD_EX), .WE_SR_OUT(WE_SR_EX), .ST_SR_OUT(ST_SR_EX));
  V_ID_EX v_id_ex_1 (
    .NOP(nop), .RESET(in_3), .CLK(CLK), .WE_VR(WE_V), .ST_VR(ST_V), .OP_ULA(OP_ULA), .R1_IN(R1_0_OUT),
    .IMM(IMM), .RA_VR(RA_0_OUT), .RB_VR(RB_0_OUT), .R1_OUT(R1_0_OUT_EX), .IMM_OUT(IMM_V_EX),
    .OP_ULA_OUT(OP_V_ULA_EX), .RA_VR_OUT(RA_0_OUT_EX), .RB_VR_OUT(RB_0_OUT_EX), .WE_VR_OUT(WE_V_EX),
    .ST_VR_OUT(ST_V_EX));
  V_ID_EX v_id_ex_2 (
    .NOP(nop), .RESET(in_3), .CLK(CLK), .WE_VR(WE_V), .ST_VR(ST_V), .OP_ULA(OP_ULA), .R1_IN(R1_1_OUT),
    .IMM(IMM), .RA_VR(RA_1_OUT), .RB_VR(RB_1_OUT), .R1_OUT(R1_1_OUT_EX), .IMM_OUT(IMM_V_EX),
    .OP_ULA_OUT(OP_V_ULA_EX), .RA_VR_OUT(RA_1_OUT_EX), .RB_VR_OUT(RB_1_OUT_EX), .WE_VR_OUT(WE_V_EX),
    .ST_VR_OUT(ST_V_EX));
  V_ID_EX v_id_ex_3 (
    .NOP(nop), .RESET(in_3), .CLK(CLK), .WE_VR(WE_V), .ST_VR(ST_V), .OP_ULA(OP_ULA), .R1_IN(R1_2_OUT),
    .IMM(IMM), .RA_VR(RA_2_OUT), .RB_VR(RB_2_OUT), .R1_OUT(R1_2_OUT_EX), .IMM_OUT(IMM_V_EX),
    .OP_ULA_OUT(OP_V_ULA_EX), .RA_VR_OUT(RA_2_OUT_EX), .RB_VR_OUT(RB_2_OUT_EX), .WE_VR_OUT(WE_V_EX),
    .ST_VR_OUT(ST_V_EX));
  V_ID_EX v_id_ex_4 (
    .NOP(nop), .RESET(in_3), .CLK(CLK), .WE_VR(WE_V), .ST_VR(ST_V), .OP_ULA(OP_ULA), .R1_IN(R1_3_OUT),
    .IMM(IMM), .RA_VR(RA_3_OUT), .RB_VR(RB_3_OUT), .R1_OUT(R1_3_OUT_EX), .IMM_OUT(IMM_V_EX),
    .OP_ULA_OUT(OP_V_ULA_EX), .RA_VR_OUT(RA_3_OUT_EX), .RB_VR_OUT(RB_3_OUT_EX), .WE_VR_OUT(WE_V_EX),
    .ST_VR_OUT(ST_V_EX));
  Multiplexer #(.select(2), .width(8)) multiplexer_10 (
    .in0(RA_OUT_SR_EX), .in1(DATA_WB), .in2(ULA_RESULT_SR_MEM), .out(RA_ULA), .sel(F_RA));  // open: in3
  Multiplexer #(.select(2), .width(8)) multiplexer_11 (
    .in0(RB_OUT_SR_EX), .in1(DATA_WB), .in2(ULA_RESULT_SR_MEM), .out(RB_ULA), .sel(F_RB));  // open: in3
  Multiplexer #(.select(2), .width(8)) multiplexer_12 (
    .in0(R1_OUT_SR_EX), .in1(DATA_WB), .in2(ULA_RESULT_SR_MEM), .out(R1_ULA), .sel(F_R1));  // open: in3
  Multiplexer #(.select(2), .width(8)) multiplexer_13 (
    .in0(RA_0_OUT_EX), .in1(DATA_V0_WB), .in2(ULA_RESULT_0_MEM), .out(RA_V0_ULA), .sel(F_V_RA));  // open: in3
  Multiplexer #(.select(2), .width(8)) multiplexer_14 (
    .in0(RB_0_OUT_EX), .in1(DATA_V0_WB), .in2(ULA_RESULT_0_MEM), .out(RB_V0_ULA), .sel(F_V_RB));  // open: in3
  Multiplexer #(.select(2), .width(8)) multiplexer_15 (
    .in0(R1_0_OUT_EX), .in1(DATA_V0_WB), .in2(ULA_RESULT_0_MEM), .out(R1_V0_ULA), .sel(F_V_R1));  // open: in3
  Multiplexer #(.select(2), .width(8)) multiplexer_16 (
    .in0(RA_1_OUT_EX), .in1(DATA_V1_WB), .in2(ULA_RESULT_1_MEM), .out(RA_V1_ULA), .sel(F_V_RA));  // open: in3
  Multiplexer #(.select(2), .width(8)) multiplexer_17 (
    .in0(RB_1_OUT_EX), .in1(DATA_V1_WB), .in2(ULA_RESULT_1_MEM), .out(RB_V1_ULA), .sel(F_V_RB));  // open: in3
  Multiplexer #(.select(2), .width(8)) multiplexer_18 (
    .in0(R1_1_OUT_EX), .in1(DATA_V1_WB), .in2(ULA_RESULT_1_MEM), .out(R1_V1_ULA), .sel(F_V_R1));  // open: in3
  Multiplexer #(.select(2), .width(8)) multiplexer_19 (
    .in0(RA_2_OUT_EX), .in1(DATA_V2_WB), .in2(ULA_RESULT_2_MEM), .out(RA_V2_ULA), .sel(F_V_RA));  // open: in3
  Multiplexer #(.select(2), .width(8)) multiplexer_20 (
    .in0(RB_2_OUT_EX), .in1(DATA_V2_WB), .in2(ULA_RESULT_2_MEM), .out(RB_V2_ULA), .sel(F_V_RB));  // open: in3
  Multiplexer #(.select(2), .width(8)) multiplexer_21 (
    .in0(R1_2_OUT_EX), .in1(DATA_V2_WB), .in2(ULA_RESULT_2_MEM), .out(R1_V2_ULA), .sel(F_V_R1));  // open: in3
  Multiplexer #(.select(2), .width(8)) multiplexer_22 (
    .in0(RA_3_OUT_EX), .in1(DATA_V3_WB), .in2(ULA_RESULT_3_MEM), .out(RA_V3_ULA), .sel(F_V_RA));  // open: in3
  Multiplexer #(.select(2), .width(8)) multiplexer_23 (
    .in0(RB_3_OUT_EX), .in1(DATA_V3_WB), .in2(ULA_RESULT_3_MEM), .out(RB_V3_ULA), .sel(F_V_RB));  // open: in3
  Multiplexer #(.select(2), .width(8)) multiplexer_24 (
    .in0(R1_3_OUT_EX), .in1(DATA_V3_WB), .in2(ULA_RESULT_3_MEM), .out(R1_V3_ULA), .sel(F_V_R1));  // open: in3
  FOW_UNIT_ULA fow_unit_ula_1 (
    .RD_MEM(RD_MEM), .RA(RA_EX), .RB(RB_EX), .WE_MEM(WE_V_MEM), .WE_WB(WE_V_WB), .RD_WB(RD_WB),
    .FORW_A(F_V_RA), .FOW_B(F_V_RB), .FOW_1(F_V_R1));
  FOW_UNIT_ULA fow_unit_ula_2 (
    .RD_MEM(RD_MEM), .RA(RA_EX), .RB(RB_EX), .WE_MEM(WE_SR_MEM), .WE_WB(WE_SR_WB), .RD_WB(RD_WB),
    .FORW_A(F_RA), .FOW_B(F_RB), .FOW_1(F_R1));
  ULA ula_1 (
    .RA(RA_ULA), .RB(RB_ULA), .INC_OPS(INC_OPS_EX), .op_ula(OP_ULA_EX), .R1(R1_ULA), .IMM(IMM_EX),
    .ULA_RESULT(ULA_RESULT_SR));
  VETORIAL_ULA vetorial_ula_1 (
    .RA(RA_V0_ULA), .RB(RB_V0_ULA), .op_ula(OP_V_ULA_EX), .R1(R1_V0_ULA), .IMM(IMM_V_EX),
    .ULA_RESULT(ULA_RESULT_0));
  VETORIAL_ULA vetorial_ula_2 (
    .RA(RA_V1_ULA), .RB(RB_V1_ULA), .op_ula(OP_V_ULA_EX), .R1(R1_V1_ULA), .IMM(IMM_V_EX),
    .ULA_RESULT(ULA_RESULT_1));
  VETORIAL_ULA vetorial_ula_3 (
    .RA(RA_V2_ULA), .RB(RB_V2_ULA), .op_ula(OP_V_ULA_EX), .R1(R1_V2_ULA), .IMM(IMM_V_EX),
    .ULA_RESULT(ULA_RESULT_2));
  VETORIAL_ULA vetorial_ula_4 (
    .RA(RA_V3_ULA), .RB(RB_V3_ULA), .op_ula(OP_V_ULA_EX), .R1(R1_V3_ULA), .IMM(IMM_V_EX),
    .ULA_RESULT(ULA_RESULT_3));
  EX_MEM ex_mem_1 (
    .CLK(CLK), .RESET(in_3), .LD_IN(LD_EX), .WE_IN(WE_SR_EX), .ST_IN(ST_SR_EX), .RD_IN(RD_EX),
    .RA_IN(RA_ULA), .ULA_IN(ULA_RESULT_SR), .RB_IN(RB_ULA), .RD_OUT(RD_MEM), .LD_OUT(LD_MEM),
    .WE_OUT(WE_SR_MEM), .ST_OUT(ST_SR_MEM), .RA_OUT(RA_OUT_SR_MEM), .ULA_OUT(ULA_RESULT_SR_MEM),
    .RB_OUT(RB_OUT_SR_MEM));
  V_EX_MEM v_ex_mem_1 (
    .CLK(CLK), .RESET(in_3), .WE_IN(WE_V_EX), .ST_IN(ST_V_EX), .RA_IN(RA_V0_ULA), .ULA_IN(ULA_RESULT_0),
    .RB_IN(RB_V0_ULA), .WE_OUT(WE_V_MEM), .ST_OUT(ST_V_MEM), .RA_OUT(RA_V0_MEM), .ULA_OUT(ULA_RESULT_0_MEM),
    .RB_OUT(RB_V0_MEM));
  V_EX_MEM v_ex_mem_2 (
    .CLK(CLK), .RESET(in_3), .WE_IN(WE_V_EX), .ST_IN(ST_V_EX), .RA_IN(RA_V1_ULA), .ULA_IN(ULA_RESULT_1),
    .RB_IN(RB_V1_ULA), .WE_OUT(WE_V_MEM), .ST_OUT(ST_V_MEM), .RA_OUT(RA_V1_MEM), .ULA_OUT(ULA_RESULT_1_MEM),
    .RB_OUT(RB_V1_MEM));
  V_EX_MEM v_ex_mem_3 (
    .CLK(CLK), .RESET(in_3), .WE_IN(WE_V_EX), .ST_IN(ST_V_EX), .RA_IN(RA_V2_ULA), .ULA_IN(ULA_RESULT_2),
    .RB_IN(RB_V2_ULA), .WE_OUT(WE_V_MEM), .ST_OUT(ST_V_MEM), .RA_OUT(RA_V2_MEM), .ULA_OUT(ULA_RESULT_2_MEM),
    .RB_OUT(RB_V2_MEM));
  V_EX_MEM v_ex_mem_4 (
    .CLK(CLK), .RESET(in_3), .WE_IN(WE_V_EX), .ST_IN(ST_V_EX), .RA_IN(RA_V3_ULA), .ULA_IN(ULA_RESULT_3),
    .RB_IN(RB_V3_ULA), .WE_OUT(WE_V_MEM), .ST_OUT(ST_V_MEM), .RA_OUT(RA_V3_MEM), .ULA_OUT(ULA_RESULT_3_MEM),
    .RB_OUT(RB_V3_MEM));
  RAM #(.asyncread("true")) ram_1 (
    .addr(RB_V0_MEM), .we(ST_V_MEM), .oe(1'b1), .clk(CLK), .din(RA_V0_MEM), .dout(MEM_OUT_0));
  RAM #(.asyncread("true")) ram_2 (
    .addr(RB_V1_MEM), .we(ST_V_MEM), .oe(1'b1), .clk(CLK), .din(RA_V1_MEM), .dout(MEM_OUT_1));
  RAM #(.asyncread("true")) ram_3 (
    .addr(RB_V2_MEM), .we(ST_V_MEM), .oe(1'b1), .clk(CLK), .din(RA_V2_MEM), .dout(MEM_OUT_2));
  RAM #(.asyncread("true")) ram_4 (
    .addr(RB_V3_MEM), .we(ST_V_MEM), .oe(1'b1), .clk(CLK), .din(RA_V3_MEM), .dout(MEM_OUT_3));
  RAM #(.asyncread("true")) ram_5 (
    .addr(RB_OUT_SR_MEM), .we(ST_SR_MEM), .oe(1'b1), .clk(CLK), .din(RA_OUT_SR_MEM), .dout(MEM_OUT_SR));
  MEM_WB mem_wb_1 (
    .CLK(CLK), .RESET(in_3), .LD_IN(LD_MEM), .WE_IN(WE_SR_MEM), .RD_IN(RD_MEM), .MEM_DATA(MEM_OUT_SR),
    .ULA_IN(ULA_RESULT_SR_MEM), .ULA_OUT(ULA_RESULT_SR_WB), .RD_OUT(RD_WB), .LD_OUT(LD_WB),
    .WE_OUT(WE_SR_WB), .MEM_DATA_OUT(MEM_OUT_SR_WB));
  V_MEM_WB v_mem_wb_1 (
    .CLK(CLK), .RESET(in_3), .WE_IN(WE_V_MEM), .MEM_DATA(MEM_OUT_0), .ULA_IN(ULA_RESULT_0_MEM),
    .ULA_OUT(ULA_RESULT_0_WB), .WE_OUT(WE_V_WB), .MEM_DATA_OUT(MEM_V0_WB));
  V_MEM_WB v_mem_wb_2 (
    .CLK(CLK), .RESET(in_3), .WE_IN(WE_V_MEM), .MEM_DATA(MEM_OUT_1), .ULA_IN(ULA_RESULT_1_MEM),
    .ULA_OUT(ULA_RESULT_1_WB), .WE_OUT(WE_V_WB), .MEM_DATA_OUT(MEM_V1_WB));
  V_MEM_WB v_mem_wb_3 (
    .CLK(CLK), .RESET(in_3), .WE_IN(WE_V_MEM), .MEM_DATA(MEM_OUT_2), .ULA_IN(ULA_RESULT_2_MEM),
    .ULA_OUT(ULA_RESULT_2_WB), .WE_OUT(WE_V_WB), .MEM_DATA_OUT(MEM_V2_WB));
  V_MEM_WB v_mem_wb_4 (
    .CLK(CLK), .RESET(in_3), .WE_IN(WE_V_MEM), .MEM_DATA(MEM_OUT_3), .ULA_IN(ULA_RESULT_3_MEM),
    .ULA_OUT(ULA_RESULT_3_WB), .WE_OUT(WE_V_WB), .MEM_DATA_OUT(MEM_V3_WB));
  Multiplexer #(.width(8)) multiplexer_25 (.in0(ULA_RESULT_0_WB), .in1(MEM_V0_WB), .out(DATA_V0_WB), .sel(LD_WB));
  Multiplexer #(.width(8)) multiplexer_26 (.in0(ULA_RESULT_SR_WB), .in1(MEM_OUT_SR_WB), .out(DATA_WB), .sel(LD_WB));
  Multiplexer #(.width(8)) multiplexer_27 (.in0(ULA_RESULT_1_WB), .in1(MEM_V1_WB), .out(DATA_V1_WB), .sel(LD_WB));
  Multiplexer #(.width(8)) multiplexer_28 (.in0(ULA_RESULT_2_WB), .in1(MEM_V2_WB), .out(DATA_V2_WB), .sel(LD_WB));
  Multiplexer #(.width(8)) multiplexer_29 (.in0(ULA_RESULT_3_WB), .in1(MEM_V3_WB), .out(DATA_V3_WB), .sel(LD_WB));

  // Other names for the same wires on the sheet: INC_OPS[1:0] = IMM[1:0]; RB[1:0] = IMM[1:0]; RA[1:0] = IMM[3:2];
  //   RESET = in_3

  // Notes on the sheet:
  //   contents of rom_1 (hex, n*v repeats v):
  //   68 6c a0 b4 cd b0 a8 c9 c8 d5 c4 33 49 32 f6 96 c7 cb a1 b4 c4 f6 96 c7 cb d5 da df 55 5a 5f a8 cd
  //   cc d5 3e 49 32 f6 8b bc cd 87 c9 a0 bc cd 9b dd dd b4 cd 23 36 71
  //   contents of rom_2 (hex, n*v repeats v):
  //   10f 407 142 143 104 105 106 17 8f 207 c2 c3 84 85 100 27
endmodule

module banco_reg (
  input  WE,
  input  Reset,
  input  CLK,
  input  [1:0] RA,
  input  [1:0] RD,
  input  [1:0] RB,
  input  [7:0] DATA,
  output [7:0] R1_OUT,
  output [7:0] RA_OUT,
  output [7:0] RB_OUT
);

  wire W_R1, W_R2, W_R3;
  wire [7:0] R2, R3;

  Register #(.trigger("falling")) R1 (.D(DATA), .en(W_R1), .clk(CLK), .Q(R1_OUT), .clr(Reset));
  Demultiplexer #(.select(2)) demultiplexer_1 (.out1(W_R1), .out2(W_R2), .out3(W_R3), .in(WE), .sel(RD));  // open: out0
  Register #(.trigger("falling")) u_R2 (.D(DATA), .en(W_R2), .clk(CLK), .Q(R2), .clr(Reset));
  Register #(.trigger("falling")) u_R3 (.D(DATA), .en(W_R3), .clk(CLK), .Q(R3), .clr(Reset));
  Multiplexer #(.select(2), .width(8)) multiplexer_1 (
    .in0({8{1'b0}}), .in1(R1_OUT), .in2(R2), .in3(R3), .out(RA_OUT), .sel(RA));
  Multiplexer #(.select(2), .width(8)) multiplexer_2 (
    .in0({8{1'b0}}), .in1(R1_OUT), .in2(R2), .in3(R3), .out(RB_OUT), .sel(RB));

  // Other names for the same wires on the sheet: CLK_t = CLK; R1[7:0] = R1_OUT; R_t = Reset
endmodule

module ULA (
  input  [1:0] INC_OPS,
  input  [3:0] IMM,
  input  [2:0] op_ula,
  input  [7:0] R1,
  input  [7:0] RA,
  input  [7:0] RB,
  output [7:0] ULA_RESULT
);

  wire [7:0] adder_1_out, adder_2_out, adder_3_out, adder_4_out, and_1_out, bit_extender_1_out,
       bit_extender_2_out, bit_extender_3_out, multiplexer_1_out, not_1_out, or_1_out, shifter_1_out,
       shifter_2_out, subtractor_1_out, subtractor_2_out;

  assign bit_extender_1_out = {{4{1'b0}}, R1[3:0]};  // Bit_Extender bit_extender_1
  assign bit_extender_2_out = {{4{1'b0}}, R1[7:4]};  // Bit_Extender bit_extender_2
  assign bit_extender_3_out = {{4{1'b0}}, IMM};  // Bit_Extender bit_extender_3
  Shifter shifter_1 (.in(bit_extender_3_out), .\dist (3'b100), .out(shifter_1_out));
  Shifter shifter_2 (.in(bit_extender_2_out), .\dist (3'b100), .out(shifter_2_out));
  Adder adder_1 (.a(RA), .b(RB), .out(adder_1_out));  // open: cin, cout
  Subtractor subtractor_1 (.a(RA), .b(RB), .out(subtractor_1_out));  // open: bin, bout
  assign and_1_out = RA & RB;  // AND_Gate and_1, 8 bits wide
  Adder adder_2 (.a(RA), .b(8'h1), .out(adder_2_out));  // open: cin, cout
  assign or_1_out = R1 | RA;  // OR_Gate or_1, 8 bits wide
  Subtractor subtractor_2 (.a(RA), .b(8'h1), .out(subtractor_2_out));  // open: bin, bout
  assign not_1_out = ~R1;  // NOT_Gate not_1, 8 bits wide
  Adder adder_3 (.a(bit_extender_1_out), .b(shifter_1_out), .out(adder_3_out));  // open: cin, cout
  Adder adder_4 (.a(bit_extender_3_out), .b(shifter_2_out), .out(adder_4_out));  // open: cin, cout
  Multiplexer #(.select(2), .width(8)) multiplexer_1 (
    .in0(not_1_out), .in1(adder_2_out), .in2(or_1_out), .in3(subtractor_2_out), .out(multiplexer_1_out),
    .sel(INC_OPS));
  Multiplexer #(.select(3), .width(8)) multiplexer_2 (
    .in0(multiplexer_1_out), .in1({8{1'b0}}), .in2(adder_3_out), .in3(adder_4_out), .in4(adder_1_out),
    .in5(subtractor_1_out), .in6(and_1_out), .in7({8{1'b0}}), .out(ULA_RESULT), .sel(op_ula));
endmodule

module dual_port_ram (
  input  [7:0] addr,
  input  [7:0] pc,
  input  [7:0] d,
  input  w,
  output [7:0] instr,
  output [7:0] data
);

  wire clock_1_out, or_1_out;
  wire [7:0] multiplexer_1_out;

  Clock clock_1 (.out(clock_1_out));
  or or_1 (or_1_out, w, clock_1_out);
  Multiplexer #(.width(8)) multiplexer_1 (.in0(addr), .in1(pc), .out(multiplexer_1_out), .sel(clock_1_out));
  RAM #(.asyncread("true")) ram_1 (
    .addr(multiplexer_1_out), .we(or_1_out), .oe(1'b1), .clk(clock_1_out), .din(d), .dout(data));
  Register #(.trigger("falling")) pcbuf (.D(data), .en(1'b1), .clk(clock_1_out), .Q(instr));  // open: clr
endmodule

module VETORIAL_ULA (
  input  [3:0] IMM,
  input  [2:0] op_ula,
  input  [7:0] R1,
  input  [7:0] RA,
  input  [7:0] RB,
  output [7:0] ULA_RESULT
);

  wire [7:0] adder_1_out, adder_2_out, adder_3_out, and_1_out, bit_extender_1_out, bit_extender_2_out,
       bit_extender_3_out, shifter_1_out, shifter_2_out, subtractor_1_out;

  assign bit_extender_1_out = {{4{1'b0}}, R1[3:0]};  // Bit_Extender bit_extender_1
  assign bit_extender_2_out = {{4{1'b0}}, R1[7:4]};  // Bit_Extender bit_extender_2
  assign bit_extender_3_out = {{4{1'b0}}, IMM};  // Bit_Extender bit_extender_3
  Shifter shifter_1 (.in(bit_extender_3_out), .\dist (3'b100), .out(shifter_1_out));
  Shifter shifter_2 (.in(bit_extender_2_out), .\dist (3'b100), .out(shifter_2_out));
  Adder adder_1 (.a(RA), .b(RB), .out(adder_1_out));  // open: cin, cout
  Subtractor subtractor_1 (.a(RA), .b(RB), .out(subtractor_1_out));  // open: bin, bout
  assign and_1_out = RA & RB;  // AND_Gate and_1, 8 bits wide
  Adder adder_2 (.a(bit_extender_1_out), .b(shifter_1_out), .out(adder_2_out));  // open: cin, cout
  Adder adder_3 (.a(bit_extender_3_out), .b(shifter_2_out), .out(adder_3_out));  // open: cin, cout
  Multiplexer #(.select(3), .width(8)) multiplexer_1 (
    .in2(adder_2_out), .in3(adder_3_out), .in4(adder_1_out), .in5(subtractor_1_out), .in6(and_1_out),
    .in7({8{1'b0}}), .out(ULA_RESULT), .sel(op_ula));  // open: in0, in1
endmodule

module REG_BANK_VET_0 (
  input  WE,
  input  Reset,
  input  CLK,
  input  [1:0] RA,
  input  [1:0] RD,
  input  [1:0] RB,
  input  [7:0] DATA,
  output [7:0] R1_OUT,
  output [7:0] RA_OUT,
  output [7:0] RB_OUT
);

  wire W_R1, W_R2, W_R3;
  wire [7:0] R2, R3;

  Register #(.trigger("falling")) R1 (.D(DATA), .en(W_R1), .clk(CLK), .Q(R1_OUT), .clr(Reset));
  Demultiplexer #(.select(2)) demultiplexer_1 (.out1(W_R1), .out2(W_R2), .out3(W_R3), .in(WE), .sel(RD));  // open: out0
  Register #(.trigger("falling")) u_R2 (.D(DATA), .en(W_R2), .clk(CLK), .Q(R2), .clr(Reset));
  Register #(.trigger("falling")) u_R3 (.D(DATA), .en(W_R3), .clk(CLK), .Q(R3), .clr(Reset));
  Multiplexer #(.select(2), .width(8)) multiplexer_1 (
    .in0({8{1'b0}}), .in1(R1_OUT), .in2(R2), .in3(R3), .out(RA_OUT), .sel(RA));
  Multiplexer #(.select(2), .width(8)) multiplexer_2 (
    .in0({8{1'b0}}), .in1(R1_OUT), .in2(R2), .in3(R3), .out(RB_OUT), .sel(RB));

  // Other names for the same wires on the sheet: CLK_t = CLK; R1[7:0] = R1_OUT; R_t = Reset
endmodule

module REG_BANK_VET_1 (
  input  WE,
  input  Reset,
  input  CLK,
  input  [1:0] RA,
  input  [1:0] RD,
  input  [1:0] RB,
  input  [7:0] DATA,
  output [7:0] R1_OUT,
  output [7:0] RA_OUT,
  output [7:0] RB_OUT
);

  wire W_R1, W_R2, W_R3;
  wire [7:0] R2, R3;

  Register #(.trigger("falling")) R1 (.D(DATA), .en(W_R1), .clk(CLK), .Q(R1_OUT), .clr(Reset));
  Demultiplexer #(.select(2)) demultiplexer_1 (.out1(W_R1), .out2(W_R2), .out3(W_R3), .in(WE), .sel(RD));  // open: out0
  Register #(.trigger("falling")) u_R2 (.D(DATA), .en(W_R2), .clk(CLK), .Q(R2), .clr(Reset));
  Register #(.trigger("falling")) u_R3 (.D(DATA), .en(W_R3), .clk(CLK), .Q(R3), .clr(Reset));
  Multiplexer #(.select(2), .width(8)) multiplexer_1 (
    .in0(8'h1), .in1(R1_OUT), .in2(R2), .in3(R3), .out(RA_OUT), .sel(RA));
  Multiplexer #(.select(2), .width(8)) multiplexer_2 (
    .in0(8'h1), .in1(R1_OUT), .in2(R2), .in3(R3), .out(RB_OUT), .sel(RB));

  // Other names for the same wires on the sheet: CLK_t = CLK; R1[7:0] = R1_OUT; R_t = Reset
endmodule

module REG_BANK_VET_2 (
  input  WE,
  input  Reset,
  input  CLK,
  input  [1:0] RA,
  input  [1:0] RD,
  input  [1:0] RB,
  input  [7:0] DATA,
  output [7:0] R1_OUT,
  output [7:0] RA_OUT,
  output [7:0] RB_OUT
);

  wire W_R1, W_R2, W_R3;
  wire [7:0] R2, R3;

  Register #(.trigger("falling")) R1 (.D(DATA), .en(W_R1), .clk(CLK), .Q(R1_OUT), .clr(Reset));
  Demultiplexer #(.select(2)) demultiplexer_1 (.out1(W_R1), .out2(W_R2), .out3(W_R3), .in(WE), .sel(RD));  // open: out0
  Register #(.trigger("falling")) u_R2 (.D(DATA), .en(W_R2), .clk(CLK), .Q(R2), .clr(Reset));
  Register #(.trigger("falling")) u_R3 (.D(DATA), .en(W_R3), .clk(CLK), .Q(R3), .clr(Reset));
  Multiplexer #(.select(2), .width(8)) multiplexer_1 (
    .in0(8'h2), .in1(R1_OUT), .in2(R2), .in3(R3), .out(RA_OUT), .sel(RA));
  Multiplexer #(.select(2), .width(8)) multiplexer_2 (
    .in0(8'h2), .in1(R1_OUT), .in2(R2), .in3(R3), .out(RB_OUT), .sel(RB));

  // Other names for the same wires on the sheet: CLK_t = CLK; R1[7:0] = R1_OUT; R_t = Reset
endmodule

module REG_BANK_VET_3 (
  input  WE,
  input  Reset,
  input  CLK,
  input  [1:0] RA,
  input  [1:0] RD,
  input  [1:0] RB,
  input  [7:0] DATA,
  output [7:0] R1_OUT,
  output [7:0] RA_OUT,
  output [7:0] RB_OUT
);

  wire W_R1, W_R2, W_R3;
  wire [7:0] R2, R3;

  Register #(.trigger("falling")) R1 (.D(DATA), .en(W_R1), .clk(CLK), .Q(R1_OUT), .clr(Reset));
  Demultiplexer #(.select(2)) demultiplexer_1 (.out1(W_R1), .out2(W_R2), .out3(W_R3), .in(WE), .sel(RD));  // open: out0
  Register #(.trigger("falling")) u_R2 (.D(DATA), .en(W_R2), .clk(CLK), .Q(R2), .clr(Reset));
  Register #(.trigger("falling")) u_R3 (.D(DATA), .en(W_R3), .clk(CLK), .Q(R3), .clr(Reset));
  Multiplexer #(.select(2), .width(8)) multiplexer_1 (
    .in0(8'h3), .in1(R1_OUT), .in2(R2), .in3(R3), .out(RA_OUT), .sel(RA));
  Multiplexer #(.select(2), .width(8)) multiplexer_2 (
    .in0(8'h3), .in1(R1_OUT), .in2(R2), .in3(R3), .out(RB_OUT), .sel(RB));

  // Other names for the same wires on the sheet: CLK_t = CLK; R1[7:0] = R1_OUT; R_t = Reset
endmodule

module CONTROL_UNIT (
  input  BIT_1,
  input  BIT_2,
  input  BIT_3,
  input  BIT_4,
  output [2:0] OP_ULA,
  output LOAD,
  output BRANCH,
  output REP,
  output MOV,
  output WE_V,
  output WE_SR,
  output STORE_V,
  output STORE_SR
);

  wire and_1_out, and_3_out, and_4_out, and_9_out, and_10_out, and_11_out, not_5_out, not_6_out, not_7_out,
       NOT_BIT_1, NOT_BIT_2, NOT_BIT_3, NOT_BIT_4, or_1_out, or_2_out;

  not not_1 (NOT_BIT_1, BIT_1);
  not not_2 (NOT_BIT_2, BIT_2);
  not not_3 (NOT_BIT_3, BIT_3);
  not not_4 (NOT_BIT_4, BIT_4);
  or or_1 (or_1_out, NOT_BIT_1, BIT_1);
  and and_1 (and_1_out, BIT_2, NOT_BIT_3);
  and and_2 (MOV, or_1_out, and_1_out);
  and and_3 (and_3_out, BIT_1, BIT_2, BIT_3);
  and and_4 (and_4_out, BIT_1, NOT_BIT_2, NOT_BIT_3);
  not not_5 (not_5_out, REP);
  and and_5 (BRANCH, not_5_out, and_3_out);
  or or_2 (or_2_out, and_3_out, and_4_out);
  not not_6 (not_6_out, or_2_out);
  and and_6 (REP, BIT_1, BIT_2, BIT_3, BIT_4);
  and and_7 (STORE_V, BIT_4, and_4_out);
  and and_8 (STORE_SR, and_4_out, NOT_BIT_4);
  and and_9 (and_9_out, NOT_BIT_1, BIT_2, BIT_3, BIT_4);
  and and_10 (and_10_out, BIT_4, not_6_out);
  and and_11 (and_11_out, not_6_out, NOT_BIT_4);
  Multiplexer #(.width(3)) multiplexer_1 (.in0({BIT_3, BIT_2, BIT_1}), .in1(3'b000), .out(OP_ULA), .sel(and_9_out));
  not not_7 (not_7_out, and_9_out);
  and and_12 (WE_V, not_7_out, and_10_out);
  or or_3 (WE_SR, and_9_out, and_11_out);
  and and_13 (LOAD, NOT_BIT_1, NOT_BIT_2, NOT_BIT_3);
endmodule

module ID_EX (
  input  LD,
  input  WE_SR,
  input  ST_SR,
  input  NOP,
  input  RESET,
  input  [2:0] OP_ULA,
  input  CLK,
  input  [7:0] RA_SR,
  input  [7:0] RB_SR,
  input  [7:0] R1_IN,
  input  [3:0] IMM,
  input  [1:0] RA_ID,
  input  [1:0] RB_ID,
  input  [1:0] RD_ID,
  input  [1:0] INC_OPS,
  output LD_OUT,
  output WE_SR_OUT,
  output ST_SR_OUT,
  output [2:0] OP_ULA_OUT,
  output [7:0] RA_SR_OUT,
  output [7:0] RB_SR_OUT,
  output [7:0] R1_OUT,
  output [3:0] IMM_OUT,
  output [1:0] RA_OUT,
  output [1:0] RB_OUT,
  output [1:0] RD_OUT,
  output [1:0] INC_OPS_OUT
);

  wire multiplexer_1_out, multiplexer_2_out, multiplexer_3_out;
  wire [2:0] multiplexer_4_out;

  Register #(.width(1)) register_1 (.D(multiplexer_1_out), .en(1'b1), .clk(CLK), .Q(LD_OUT), .clr(RESET));
  Multiplexer multiplexer_1 (.in0(LD), .in1(1'b0), .out(multiplexer_1_out), .sel(NOP));
  Register #(.width(1)) register_2 (.D(multiplexer_2_out), .en(1'b1), .clk(CLK), .Q(WE_SR_OUT), .clr(RESET));
  Multiplexer multiplexer_2 (.in0(WE_SR), .in1(1'b0), .out(multiplexer_2_out), .sel(NOP));
  Register #(.width(1)) register_3 (.D(multiplexer_3_out), .en(1'b1), .clk(CLK), .Q(ST_SR_OUT), .clr(RESET));
  Multiplexer multiplexer_3 (.in0(ST_SR), .in1(1'b0), .out(multiplexer_3_out), .sel(NOP));
  Register #(.width(3)) register_4 (.D(multiplexer_4_out), .en(1'b1), .clk(CLK), .Q(OP_ULA_OUT), .clr(RESET));
  Multiplexer #(.width(3)) multiplexer_4 (.in0(OP_ULA), .in1(3'b000), .out(multiplexer_4_out), .sel(NOP));
  Register register_5 (.D(RA_SR), .en(1'b1), .clk(CLK), .Q(RA_SR_OUT), .clr(RESET));
  Register register_6 (.D(RB_SR), .en(1'b1), .clk(CLK), .Q(RB_SR_OUT), .clr(RESET));
  Register register_7 (.D(R1_IN), .en(1'b1), .clk(CLK), .Q(R1_OUT), .clr(RESET));
  Register #(.width(4)) register_8 (.D(IMM), .en(1'b1), .clk(CLK), .Q(IMM_OUT), .clr(RESET));
  Register #(.width(2)) register_9 (.D(RA_ID), .en(1'b1), .clk(CLK), .Q(RA_OUT), .clr(RESET));
  Register #(.width(2)) register_10 (.D(RB_ID), .en(1'b1), .clk(CLK), .Q(RB_OUT), .clr(RESET));
  Register #(.width(2)) register_11 (.D(RD_ID), .en(1'b1), .clk(CLK), .Q(RD_OUT), .clr(RESET));
  Register #(.width(2)) register_12 (.D(INC_OPS), .en(1'b1), .clk(CLK), .Q(INC_OPS_OUT), .clr(RESET));
endmodule

module IF_ID (
  input  WE,
  input  [7:0] INSTRUCTION_IN,
  input  clk,
  input  NOP,
  input  RESET,
  output [7:0] INSTRUCTION_OUT
);

  wire [7:0] multiplexer_1_out;

  Multiplexer #(.width(8)) multiplexer_1 (.in0(INSTRUCTION_IN), .in1(8'h48), .out(multiplexer_1_out), .sel(NOP));
  Register register_1 (.D(multiplexer_1_out), .en(WE), .clk(clk), .Q(INSTRUCTION_OUT), .clr(RESET));
endmodule

module EX_MEM (
  input  LD_IN,
  input  WE_IN,
  input  ST_IN,
  input  [7:0] RA_IN,
  input  [7:0] ULA_IN,
  input  CLK,
  input  RESET,
  input  [7:0] RB_IN,
  input  [1:0] RD_IN,
  output LD_OUT,
  output WE_OUT,
  output ST_OUT,
  output [7:0] RA_OUT,
  output [7:0] ULA_OUT,
  output [7:0] RB_OUT,
  output [1:0] RD_OUT
);

  Register #(.width(1)) register_1 (.D(LD_IN), .en(1'b1), .clk(CLK), .Q(LD_OUT), .clr(RESET));
  Register #(.width(1)) register_2 (.D(WE_IN), .en(1'b1), .clk(CLK), .Q(WE_OUT), .clr(RESET));
  Register #(.width(1)) register_3 (.D(ST_IN), .en(1'b1), .clk(CLK), .Q(ST_OUT), .clr(RESET));
  Register register_4 (.D(RA_IN), .en(1'b1), .clk(CLK), .Q(RA_OUT), .clr(RESET));
  Register register_5 (.D(ULA_IN), .en(1'b1), .clk(CLK), .Q(ULA_OUT), .clr(RESET));
  Register register_6 (.D(RB_IN), .en(1'b1), .clk(CLK), .Q(RB_OUT), .clr(RESET));
  Register #(.width(2)) register_7 (.D(RD_IN), .en(1'b1), .clk(CLK), .Q(RD_OUT), .clr(RESET));
endmodule

module backup_pipe_exmem (
);

  wire CLK, LD_EX, LD_MEM, RESET, ST_SR_EX, ST_SR_MEM, WE_SR_EX, WE_SR_MEM;
  wire [1:0] RD_EX, RD_MEM;
  wire [7:0] RA_OUT_SR_EX, RA_OUT_SR_MEM, RB_OUT_SR_EX, RB_OUT_SR_MEM, ULA_RESULT_SR, ULA_RESULT_SR_MEM;

  Register #(.width(1)) register_1 (.D(LD_EX), .en(1'b1), .clk(CLK), .Q(LD_MEM), .clr(RESET));
  Register #(.width(1)) register_2 (.D(WE_SR_EX), .en(1'b1), .clk(CLK), .Q(WE_SR_MEM), .clr(RESET));
  Register #(.width(1)) register_3 (.D(ST_SR_EX), .en(1'b1), .clk(CLK), .Q(ST_SR_MEM), .clr(RESET));
  Register register_4 (.D(RA_OUT_SR_EX), .en(1'b1), .clk(CLK), .Q(RA_OUT_SR_MEM), .clr(RESET));
  Register register_5 (.D(ULA_RESULT_SR), .en(1'b1), .clk(CLK), .Q(ULA_RESULT_SR_MEM), .clr(RESET));
  Register register_6 (.D(RB_OUT_SR_EX), .en(1'b1), .clk(CLK), .Q(RB_OUT_SR_MEM), .clr(RESET));
  Register #(.width(2)) register_7 (.D(RD_EX), .en(1'b1), .clk(CLK), .Q(RD_MEM), .clr(RESET));
endmodule

module MEM_WB (
  input  LD_IN,
  input  WE_IN,
  input  [7:0] MEM_DATA,
  input  CLK,
  input  [7:0] ULA_IN,
  input  RESET,
  input  [1:0] RD_IN,
  output LD_OUT,
  output WE_OUT,
  output [7:0] MEM_DATA_OUT,
  output [7:0] ULA_OUT,
  output [1:0] RD_OUT
);

  Register #(.width(1)) register_1 (.D(LD_IN), .en(1'b1), .clk(CLK), .Q(LD_OUT), .clr(RESET));
  Register #(.width(1)) register_2 (.D(WE_IN), .en(1'b1), .clk(CLK), .Q(WE_OUT), .clr(RESET));
  Register register_3 (.D(MEM_DATA), .en(1'b1), .clk(CLK), .Q(MEM_DATA_OUT), .clr(RESET));
  Register register_4 (.D(ULA_IN), .en(1'b1), .clk(CLK), .Q(ULA_OUT), .clr(RESET));
  Register #(.width(2)) register_5 (.D(RD_IN), .en(1'b1), .clk(CLK), .Q(RD_OUT), .clr(RESET));
endmodule

module BACKUP_MEMWB (
);

  wire CLK, LD_MEM, LD_WB, RESET, WE_SR_MEM, WE_SR_WB;
  wire [1:0] RD_MEM, RD_WB;
  wire [7:0] register_3_q, ULA_RESULT_SR_MEM, ULA_RESULT_SR_WB, undriven;

  Register #(.width(1)) register_1 (.D(LD_MEM), .en(1'b1), .clk(CLK), .Q(LD_WB), .clr(RESET));
  Register #(.width(1)) register_2 (.D(WE_SR_MEM), .en(1'b1), .clk(CLK), .Q(WE_SR_WB), .clr(RESET));
  Register register_3 (.D(undriven), .en(1'b1), .clk(CLK), .Q(register_3_q));  // open: clr
  Register register_4 (.D(ULA_RESULT_SR_MEM), .en(1'b1), .clk(CLK), .Q(ULA_RESULT_SR_WB));  // open: clr
  Register #(.width(2)) register_5 (.D(RD_MEM), .en(1'b1), .clk(CLK), .Q(RD_WB));  // open: clr
endmodule

module HAZARD_UNIT (
  input  [1:0] RA_id,
  input  [1:0] RD_ex,
  input  [1:0] RB_id,
  input  LD_EX,
  input  BRZR,
  output nop,
  output WE_IF
);

  wire and_1_out, comparator_1_eq, comparator_2_eq, or_1_out;

  Comparator #(.mode("unsigned"), .width(2)) comparator_1 (.a(RA_id), .b(RD_ex), .eq(comparator_1_eq));  // open: gt, lt
  Comparator #(.mode("unsigned"), .width(2)) comparator_2 (.a(RB_id), .b(RD_ex), .eq(comparator_2_eq));  // open: gt, lt
  or or_1 (or_1_out, comparator_1_eq, comparator_2_eq);
  and and_1 (and_1_out, or_1_out, LD_EX);
  not not_1 (WE_IF, and_1_out);
  or or_2 (nop, and_1_out, BRZR);
endmodule

module FOW_UNIT_ULA (
  input  [1:0] RA,
  input  [1:0] RD_MEM,
  input  WE_MEM,
  input  WE_WB,
  input  [1:0] RB,
  input  [1:0] RD_WB,
  output [1:0] FORW_A,
  output [1:0] FOW_B,
  output [1:0] FOW_1
);

  wire comparator_1_eq, comparator_2_eq, comparator_3_eq, comparator_4_eq, comparator_5_eq, comparator_6_eq,
       comparator_7_eq, comparator_8_eq, comparator_9_eq;
  wire [0:0] and_2_out, and_4_out, and_6_out;
  wire [1:1] and_1_out, and_3_out, and_5_out;

  Comparator #(.mode("unsigned"), .width(2)) comparator_1 (.a(RA), .b(RD_MEM), .eq(comparator_1_eq));  // open: gt, lt
  Comparator #(.mode("unsigned"), .width(2)) comparator_2 (.a(RA), .b(RD_WB), .eq(comparator_2_eq));  // open: gt, lt
  Comparator #(.mode("unsigned"), .width(2)) comparator_3 (.a(RB), .b(RD_MEM), .eq(comparator_3_eq));  // open: gt, lt
  Comparator #(.mode("unsigned"), .width(2)) comparator_4 (.a(RB), .b(RD_WB), .eq(comparator_4_eq));  // open: gt, lt
  Comparator #(.mode("unsigned"), .width(2)) comparator_5 (
    .a(2'b01), .b(RD_MEM), .eq(comparator_5_eq));  // open: gt, lt
  Comparator #(.mode("unsigned"), .width(2)) comparator_6 (.a(2'b01), .b(RD_WB), .eq(comparator_6_eq));  // open: gt, lt
  and and_1 (and_1_out[1], comparator_1_eq, WE_MEM);
  and and_2 (and_2_out[0], comparator_2_eq, WE_WB);
  and and_3 (and_3_out[1], comparator_3_eq, WE_MEM);
  and and_4 (and_4_out[0], comparator_4_eq, WE_WB);
  and and_5 (and_5_out[1], comparator_5_eq, WE_MEM);
  and and_6 (and_6_out[0], comparator_6_eq, WE_WB);
  Comparator #(.mode("unsigned"), .width(2)) comparator_7 (
    .a({and_1_out[1], 1'b0}), .b(2'b00), .eq(comparator_7_eq));  // open: gt, lt
  Comparator #(.mode("unsigned"), .width(2)) comparator_8 (
    .a({and_3_out[1], 1'b0}), .b(2'b00), .eq(comparator_8_eq));  // open: gt, lt
  Comparator #(.mode("unsigned"), .width(2)) comparator_9 (
    .a({and_5_out[1], 1'b0}), .b(2'b00), .eq(comparator_9_eq));  // open: gt, lt
  Multiplexer #(.width(2)) multiplexer_1 (
    .in0({and_1_out[1], 1'b0}), .in1({1'b0, and_2_out[0]}), .out(FORW_A), .sel(comparator_7_eq));
  Multiplexer #(.width(2)) multiplexer_2 (
    .in0({and_3_out[1], 1'b0}), .in1({1'b0, and_4_out[0]}), .out(FOW_B), .sel(comparator_8_eq));
  Multiplexer #(.width(2)) multiplexer_3 (
    .in0({and_5_out[1], 1'b0}), .in1({1'b0, and_6_out[0]}), .out(FOW_1), .sel(comparator_9_eq));
endmodule

module FOW_UNIT_BRANCH (
  input  WE_EX,
  input  [1:0] RD_EX,
  input  [1:0] RA_ID,
  input  [1:0] RD_MEM,
  input  WE_MEM,
  output [1:0] Forw_Br
);

  wire comparator_1_eq, comparator_2_eq, comparator_3_eq;
  wire [0:0] and_2_out;
  wire [1:1] and_1_out;

  Comparator #(.mode("unsigned"), .width(2)) comparator_1 (.a(RA_ID), .b(RD_EX), .eq(comparator_1_eq));  // open: gt, lt
  Comparator #(.mode("unsigned"), .width(2)) comparator_2 (
    .a(RA_ID), .b(RD_MEM), .eq(comparator_2_eq));  // open: gt, lt
  and and_1 (and_1_out[1], comparator_1_eq, WE_EX);
  and and_2 (and_2_out[0], comparator_2_eq, WE_MEM);
  Comparator #(.mode("unsigned"), .width(2)) comparator_3 (
    .a({and_1_out[1], 1'b0}), .b(2'b00), .eq(comparator_3_eq));  // open: gt, lt
  Multiplexer #(.width(2)) multiplexer_1 (
    .in0({and_1_out[1], 1'b0}), .in1({1'b0, and_2_out[0]}), .out(Forw_Br), .sel(comparator_3_eq));
endmodule

module BRANCH_PC (
  input  [1:0] RD_MEM,
  input  [1:0] RB_ID,
  input  WE_MEM,
  input  [7:0] RB_OUT,
  input  [7:0] ULA_RESULT,
  output [7:0] PC_BRANCH
);

  wire and_1_out, comparator_1_eq;

  Comparator #(.mode("unsigned"), .width(2)) comparator_1 (
    .a(RD_MEM), .b(RB_ID), .eq(comparator_1_eq));  // open: gt, lt
  and and_1 (and_1_out, comparator_1_eq, WE_MEM);
  Multiplexer #(.width(8)) multiplexer_1 (.in0(RB_OUT), .in1(ULA_RESULT), .out(PC_BRANCH), .sel(and_1_out));
endmodule

module V_ID_EX (
  input  WE_VR,
  input  ST_VR,
  input  NOP,
  input  RESET,
  input  [2:0] OP_ULA,
  input  CLK,
  input  [7:0] RA_VR,
  input  [7:0] RB_VR,
  input  [7:0] R1_IN,
  input  [3:0] IMM,
  output WE_VR_OUT,
  output ST_VR_OUT,
  output [2:0] OP_ULA_OUT,
  output [7:0] RA_VR_OUT,
  output [7:0] RB_VR_OUT,
  output [7:0] R1_OUT,
  output [3:0] IMM_OUT
);

  wire multiplexer_1_out, multiplexer_2_out;
  wire [2:0] multiplexer_3_out;

  Register #(.width(1)) register_1 (.D(multiplexer_1_out), .en(1'b1), .clk(CLK), .Q(WE_VR_OUT), .clr(RESET));
  Multiplexer multiplexer_1 (.in0(WE_VR), .in1(1'b0), .out(multiplexer_1_out), .sel(NOP));
  Register #(.width(1)) register_2 (.D(multiplexer_2_out), .en(1'b1), .clk(CLK), .Q(ST_VR_OUT), .clr(RESET));
  Multiplexer multiplexer_2 (.in0(ST_VR), .in1(1'b0), .out(multiplexer_2_out), .sel(NOP));
  Register #(.width(3)) register_3 (.D(multiplexer_3_out), .en(1'b1), .clk(CLK), .Q(OP_ULA_OUT), .clr(RESET));
  Multiplexer #(.width(3)) multiplexer_3 (.in0(OP_ULA), .in1(3'b000), .out(multiplexer_3_out), .sel(NOP));
  Register register_4 (.D(RA_VR), .en(1'b1), .clk(CLK), .Q(RA_VR_OUT), .clr(RESET));
  Register register_5 (.D(RB_VR), .en(1'b1), .clk(CLK), .Q(RB_VR_OUT), .clr(RESET));
  Register register_6 (.D(R1_IN), .en(1'b1), .clk(CLK), .Q(R1_OUT), .clr(RESET));
  Register #(.width(4)) register_7 (.D(IMM), .en(1'b1), .clk(CLK), .Q(IMM_OUT), .clr(RESET));
endmodule

module V_EX_MEM (
  input  WE_IN,
  input  ST_IN,
  input  [7:0] RA_IN,
  input  [7:0] ULA_IN,
  input  CLK,
  input  RESET,
  input  [7:0] RB_IN,
  output WE_OUT,
  output ST_OUT,
  output [7:0] RA_OUT,
  output [7:0] ULA_OUT,
  output [7:0] RB_OUT
);

  Register #(.width(1)) register_1 (.D(WE_IN), .en(1'b1), .clk(CLK), .Q(WE_OUT), .clr(RESET));
  Register #(.width(1)) register_2 (.D(ST_IN), .en(1'b1), .clk(CLK), .Q(ST_OUT), .clr(RESET));
  Register register_3 (.D(RA_IN), .en(1'b1), .clk(CLK), .Q(RA_OUT), .clr(RESET));
  Register register_4 (.D(ULA_IN), .en(1'b1), .clk(CLK), .Q(ULA_OUT), .clr(RESET));
  Register register_5 (.D(RB_IN), .en(1'b1), .clk(CLK), .Q(RB_OUT), .clr(RESET));
endmodule

module V_MEM_WB (
  input  WE_IN,
  input  [7:0] MEM_DATA,
  input  CLK,
  input  [7:0] ULA_IN,
  input  RESET,
  output WE_OUT,
  output [7:0] MEM_DATA_OUT,
  output [7:0] ULA_OUT
);

  Register #(.width(1)) register_1 (.D(WE_IN), .en(1'b1), .clk(CLK), .Q(WE_OUT), .clr(RESET));
  Register register_2 (.D(MEM_DATA), .en(1'b1), .clk(CLK), .Q(MEM_DATA_OUT), .clr(RESET));
  Register register_3 (.D(ULA_IN), .en(1'b1), .clk(CLK), .Q(ULA_OUT), .clr(RESET));
endmodule

module FOW_UNIT_REP (
  input  [1:0] RD_EX,
  input  [1:0] RA,
  input  [1:0] RD_MEM,
  input  WE_EX,
  input  WE_MEM,
  input  WE_WB,
  input  [1:0] RD_WB,
  input  [1:0] RB,
  output [1:0] FOW_A,
  output [1:0] FOW_B
);

  wire comparator_1_eq, comparator_2_eq, comparator_3_eq, comparator_4_eq, comparator_5_eq, comparator_6_eq,
       comparator_7_eq, comparator_9_eq, EX_RA, EX_RB, MEM_RA, MEM_RB;
  wire [0:0] and_3_out, and_6_out;
  wire [1:1] and_1_out, and_2_out, and_4_out, and_5_out;

  Comparator #(.mode("unsigned"), .width(2)) comparator_1 (.a(RD_EX), .b(RA), .eq(comparator_1_eq));  // open: gt, lt
  Comparator #(.mode("unsigned"), .width(2)) comparator_2 (.a(RA), .b(RD_MEM), .eq(comparator_2_eq));  // open: gt, lt
  Comparator #(.mode("unsigned"), .width(2)) comparator_3 (.a(RA), .b(RD_WB), .eq(comparator_3_eq));  // open: gt, lt
  Comparator #(.mode("unsigned"), .width(2)) comparator_4 (.a(RD_EX), .b(RB), .eq(comparator_4_eq));  // open: gt, lt
  Comparator #(.mode("unsigned"), .width(2)) comparator_5 (.a(RB), .b(RD_MEM), .eq(comparator_5_eq));  // open: gt, lt
  Comparator #(.mode("unsigned"), .width(2)) comparator_6 (.a(RB), .b(RD_WB), .eq(comparator_6_eq));  // open: gt, lt
  and and_1 (and_1_out[1], comparator_1_eq, WE_EX);
  and and_2 (and_2_out[1], comparator_2_eq, WE_MEM);
  and and_3 (and_3_out[0], comparator_3_eq, WE_WB);
  and and_4 (and_4_out[1], comparator_4_eq, WE_EX);
  and and_5 (and_5_out[1], comparator_5_eq, WE_MEM);
  and and_6 (and_6_out[0], comparator_6_eq, WE_WB);
  Comparator #(.mode("unsigned"), .width(2)) comparator_7 (
    .a({2{and_1_out[1]}}), .b(2'b00), .eq(comparator_7_eq));  // open: gt, lt
  Comparator #(.mode("unsigned"), .width(2)) comparator_8 (
    .a({and_2_out[1], 1'b0}), .b(2'b00), .eq(MEM_RA));  // open: gt, lt
  Comparator #(.mode("unsigned"), .width(2)) comparator_9 (
    .a({2{and_4_out[1]}}), .b(2'b00), .eq(comparator_9_eq));  // open: gt, lt
  Comparator #(.mode("unsigned"), .width(2)) comparator_10 (
    .a({and_5_out[1], 1'b0}), .b(2'b00), .eq(MEM_RB));  // open: gt, lt
  not not_1 (EX_RA, comparator_7_eq);
  not not_2 (EX_RB, comparator_9_eq);
  Multiplexer #(.select(2), .width(2)) multiplexer_1 (
    .in0({and_2_out[1], 1'b0}), .in1({1'b0, and_3_out[0]}), .in2({2{and_1_out[1]}}), .in3({2{and_1_out[1]}}),
    .out(FOW_A), .sel({EX_RA, MEM_RA}));
  Multiplexer #(.select(2), .width(2)) multiplexer_2 (
    .in0({and_5_out[1], 1'b0}), .in1({1'b0, and_6_out[0]}), .in2({2{and_4_out[1]}}), .in3({2{and_4_out[1]}}),
    .out(FOW_B), .sel({EX_RB, MEM_RB}));
endmodule
